// Logisim project desloc.circ as structural Verilog: 2 circuits, main circuit main
module main (
  input  in_1,
  input  in_2,
  input  in_3,
  input  in_4,
  input  in_5,
  input  in_6,
  input  in_7,
  input  in_8,
  input  in_9,
  input  in_10,
  input  in_11
);

  wire CLK, K0, K1, K2, multiplexer_1_out, multiplexer_2_out, multiplexer_3_out, multiplexer_4_out, Q0, Q1,
       Q2, Q3;

  Multiplexer #(.select(3), .enable("false")) multiplexer_1 (
    .in0(Q0), .in1(in_2), .in2(Q1), .in3(in_8), .in4(1'b1), .out(multiplexer_1_out), .sel({K2, K1, K0}));  // open: in5, in6, in7
  Clock clock_1 (.out(CLK));
  Register #(.width(1), .Select("low")) register_1 (.D(multiplexer_1_out), .Q(Q0), .clk(CLK), .clr(in_1));  // open: en
  Multiplexer #(.select(3), .enable("false")) multiplexer_2 (
    .in0(Q1), .in1(in_6), .in2(Q2), .in3(Q0), .in4(1'b1), .out(multiplexer_2_out), .sel({K2, K1, K0}));  // open: in5, in6, in7
  Register #(.width(1), .Select("low")) register_2 (.D(multiplexer_2_out), .Q(Q1), .clk(CLK), .clr(in_1));  // open: en
  FUNCOES funcoes_1 (.LOAD(in_9), .SHR(in_3), .SHL(in_4), .SET(in_5), .K2(K2), .K1(K1), .K0(K0));
  LED led_1 (.in(Q3));
  LED led_2 (.in(Q0));
  LED led_3 (.in(Q2));
  LED led_4 (.in(Q1));
  Multiplexer #(.select(3), .enable("false")) multiplexer_3 (
    .in0(Q2), .in1(in_10), .in2(Q3), .in3(Q1), .in4(1'b1), .out(multiplexer_3_out), .sel({K2, K1, K0}));  // open: in5, in6, in7
  Register #(.width(1), .Select("low")) register_3 (.D(multiplexer_3_out), .Q(Q2), .clk(CLK), .clr(in_1));  // open: en
  Multiplexer #(.select(3), .enable("false")) multiplexer_4 (
    .in0(Q3), .in1(in_11), .in2(in_7), .in3(Q2), .in4(1'b1), .out(multiplexer_4_out), .sel({K2, K1, K0}));  // open: in5, in6, in7
  Register #(.width(1), .Select("low")) register_4 (.D(multiplexer_4_out), .Q(Q3), .clk(CLK), .clr(in_1));  // open: en

  // Other names for the same wires on the sheet: CLR = in_1; I0 = in_2; I1 = in_6; I2 = in_10; I3 = in_11;
  //   LOAD = in_9; SET = in_5; SHL = in_4; SHL_IN = in_8; SHR = in_3; SHR_IN = in_7
endmodule

module FUNCOES (
  input  LOAD,
  input  SHR,
  input  SHL,
  input  SET,
  output K2,
  output K1,
  output K0
);

  wire and_1_out, and_2_out, and_3_out, and_4_out, and_5_out, not_1_out, not_2_out, not_3_out, not_4_out,
       not_5_out, not_6_out;

  not not_1 (not_1_out, LOAD);
  and and_1 (and_1_out, not_1_out, not_2_out);
  not not_2 (not_2_out, SHR);
  not not_3 (not_3_out, SHL);
  and and_2 (and_2_out, not_3_out, SET);
  not not_4 (not_4_out, LOAD);
  and and_3 (and_3_out, not_4_out, SHL);
  not not_5 (not_5_out, LOAD);
  and and_4 (and_4_out, not_5_out, SHR);
  not not_6 (not_6_out, SHR);
  and and_5 (and_5_out, not_6_out, SHL);
  and and_6 (K2, and_1_out, and_2_out);
  or or_1 (K1, and_3_out, and_4_out);
  or or_2 (K0, and_5_out, LOAD);
endmodule
