// Logisim project filtro_fir.circ as structural Verilog: 8 circuits, main circuit main
module main (
  input  [3:0] C,
  input  [3:0] Y,
  input  in_3,
  output [9:0] out_4
);

  wire bloco_de_controle_1_clr_r, bloco_de_controle_1_en_cod, bloco_de_controle_1_ld_out,
       bloco_de_controle_1_ld_r, bloco_de_controle_1_s_cod0, bloco_de_controle_1_s_cod1, clock_1_out;

  Clock clock_1 (.out(clock_1_out));
  bloco_de_controle bloco_de_controle_1 (
    .B(in_3), .CLK(clock_1_out), .clr_r(bloco_de_controle_1_clr_r), .ld_r(bloco_de_controle_1_ld_r),
    .ld_out(bloco_de_controle_1_ld_out), .en_cod(bloco_de_controle_1_en_cod),
    .s_cod0(bloco_de_controle_1_s_cod0), .s_cod1(bloco_de_controle_1_s_cod1));
  BLOCO_OPERACIONAL bloco_operacional_1 (
    .s_cod0(bloco_de_controle_1_s_cod0), .s_cod1(bloco_de_controle_1_s_cod1),
    .en_cod(bloco_de_controle_1_en_cod), .CLK(clock_1_out), .C(C), .Y(Y), .clr_r(bloco_de_controle_1_clr_r),
    .ld_r(bloco_de_controle_1_ld_r), .ld_out(bloco_de_controle_1_ld_out), .F(out_4));
endmodule

module RxC (
  input  [3:0] C,
  input  [3:0] Y,
  input  clr_r,
  input  ld_r,
  input  ld_c,
  input  CLK,
  output [3:0] Ym,
  output [7:0] S
);

  wire not_1_out;
  wire [3:0] register_1_q;

  Register #(.width(4), .Select("low")) register_1 (.D(C), .en(ld_c), .Q(register_1_q), .clk(CLK));  // open: clr
  Register #(.width(4), .Select("low")) register_2 (.D(Y), .en(ld_r), .Q(Ym), .clk(CLK), .clr(not_1_out));
  not not_1 (not_1_out, clr_r);
  Multiplier #(.width(4)) multiplier_1 (.a(register_1_q), .b(Ym), .out(S[3:0]), .cout(S[7:4]));  // open: cin

  // Other names for the same wires on the sheet: S2[3:0] = S[3:0]; S1[3:0] = S[7:4]
endmodule

module cod_2x4 (
  input  s_cod1,
  input  s_cod2,
  input  E,
  output s0,
  output s1,
  output s2,
  output s3
);

  wire not_1_out, not_2_out;

  not not_1 (not_1_out, s_cod1);
  not not_2 (not_2_out, s_cod2);
  and and_1 (s0, not_1_out, not_2_out, E);
  and and_2 (s1, s_cod1, not_2_out, E);
  and and_3 (s2, not_1_out, s_cod2, E);
  and and_4 (s3, s_cod1, s_cod2, E);
endmodule

module LOG_COMB (
  input  Q2,
  input  Q1,
  input  Q0,
  input  PRESS,
  output D2,
  output D1,
  output D0,
  output clr_r,
  output ld_r,
  output ld_out,
  output en_cod,
  output s_cod0,
  output s_cod1
);

  wire and_1_out, and_2_out, and_3_out, and_4_out, and_5_out, and_6_out, and_7_out, and_8_out, and_9_out,
       and_10_out, and_12_out, and_13_out, and_14_out, and_16_out, and_17_out, and_18_out, and_19_out,
       and_20_out, and_21_out, and_22_out, not_1_out, not_2_out, not_3_out, not_4_out, not_5_out, not_6_out,
       not_7_out, not_8_out, not_9_out, not_10_out, not_11_out, not_12_out, not_13_out, not_14_out,
       not_15_out, not_16_out, not_17_out, not_18_out, not_19_out, not_20_out, not_21_out, not_22_out,
       not_23_out, not_24_out, or_2_out;

  not not_1 (not_1_out, Q2);
  and and_1 (and_1_out, not_1_out, Q1);
  not not_2 (not_2_out, Q2);
  and and_2 (and_2_out, not_2_out, not_3_out);
  not not_3 (not_3_out, Q1);
  not not_4 (not_4_out, Q2);
  and and_3 (and_3_out, not_4_out, Q1);
  not not_5 (not_5_out, Q0);
  not not_6 (not_6_out, Q2);
  and and_4 (and_4_out, not_6_out, not_7_out);
  not not_7 (not_7_out, Q0);
  not not_8 (not_8_out, Q2);
  and and_5 (and_5_out, not_8_out, Q1);
  not not_9 (not_9_out, Q0);
  not not_10 (not_10_out, Q1);
  and and_6 (and_6_out, not_10_out, not_11_out);
  not not_11 (not_11_out, Q0);
  not not_12 (not_12_out, Q2);
  and and_7 (and_7_out, not_12_out, Q1);
  not not_13 (not_13_out, Q2);
  and and_8 (and_8_out, not_13_out, Q0);
  not not_14 (not_14_out, Q2);
  and and_9 (and_9_out, not_14_out, Q1);
  and and_10 (and_10_out, Q2, not_15_out);
  not not_15 (not_15_out, Q1);
  not not_16 (not_16_out, Q0);
  not not_17 (not_17_out, Q1);
  and and_11 (ld_out, not_17_out, not_18_out);
  not not_18 (not_18_out, Q0);
  not not_19 (not_19_out, Q2);
  and and_12 (and_12_out, Q2, not_20_out);
  not not_20 (not_20_out, Q1);
  not not_21 (not_21_out, Q0);
  not not_22 (not_22_out, Q2);
  and and_13 (and_13_out, not_22_out, Q1);
  and and_14 (and_14_out, Q2, not_23_out);
  not not_23 (not_23_out, Q1);
  not not_24 (not_24_out, Q0);
  and and_15 (D2, and_1_out, Q0);
  and and_16 (and_16_out, and_2_out, Q0);
  and and_17 (and_17_out, and_3_out, not_5_out);
  and and_18 (and_18_out, and_4_out, PRESS);
  and and_19 (and_19_out, and_5_out, not_9_out);
  or or_1 (clr_r, and_6_out, and_7_out);
  or or_2 (or_2_out, and_8_out, and_9_out);
  and and_20 (and_20_out, and_10_out, not_16_out);
  and and_21 (and_21_out, not_19_out, Q1);
  and and_22 (and_22_out, and_12_out, not_21_out);
  and and_23 (s_cod0, and_13_out, Q0);
  and and_24 (s_cod1, and_14_out, not_24_out);
  or or_3 (D1, and_16_out, and_17_out);
  or or_4 (D0, and_18_out, and_19_out);
  or or_5 (ld_r, or_2_out, and_20_out);
  or or_6 (en_cod, and_21_out, and_22_out);
endmodule

module bloco_de_controle (
  input  B,
  input  CLK,
  output clr_r,
  output ld_r,
  output ld_out,
  output en_cod,
  output s_cod0,
  output s_cod1
);

  wire bs_1_press, D0, D1, D2, Q0, Q1, Q2;

  BS bs_1 (.B(B), .CLK(CLK), .PRESS(bs_1_press));
  LOG_COMB log_comb_1 (
    .Q2(Q2), .Q1(Q1), .Q0(Q0), .PRESS(bs_1_press), .D2(D2), .D1(D1), .D0(D0), .clr_r(clr_r), .ld_r(ld_r),
    .ld_out(ld_out), .en_cod(en_cod), .s_cod0(s_cod0), .s_cod1(s_cod1));
  D_Flip_Flop d_ff_1 (.clk(CLK), .D(D2), .Q(Q2));  // open: Qn, preset, reset
  D_Flip_Flop d_ff_2 (.clk(CLK), .D(D1), .Q(Q1));  // open: Qn, preset, reset
  D_Flip_Flop d_ff_3 (.clk(CLK), .D(D0), .Q(Q0));  // open: Qn, preset, reset
endmodule

module BS (
  input  B,
  input  CLK,
  output PRESS
);

  wire D0, D1, Q0, Q1;

  LOG_BS log_bs_1 (.Q1(Q1), .Q0(Q0), .B(B), .D1(D1), .D0(D0), .PRESS(PRESS));
  D_Flip_Flop d_ff_1 (.clk(CLK), .D(D1), .Q(Q1));  // open: Qn, preset, reset
  D_Flip_Flop d_ff_2 (.clk(CLK), .D(D0), .Q(Q0));  // open: Qn, preset, reset
endmodule

module LOG_BS (
  input  Q1,
  input  Q0,
  input  B,
  output D1,
  output D0,
  output PRESS
);

  wire and_1_out, and_2_out, and_4_out, and_5_out, not_1_out, not_2_out, not_3_out, not_4_out, not_5_out;

  not not_1 (not_1_out, Q0);
  not not_2 (not_2_out, Q1);
  not not_3 (not_3_out, Q0);
  not not_4 (not_4_out, Q1);
  not not_5 (not_5_out, Q1);
  and and_1 (and_1_out, Q1, not_1_out);
  and and_2 (and_2_out, not_2_out, not_3_out);
  and and_3 (PRESS, not_4_out, Q0);
  and and_4 (and_4_out, not_5_out, Q0);
  and and_5 (and_5_out, and_1_out, B);
  and and_6 (D0, and_2_out, B);
  or or_1 (D1, and_4_out, and_5_out);
endmodule

module BLOCO_OPERACIONAL (
  input  s_cod0,
  input  s_cod1,
  input  en_cod,
  input  CLK,
  input  [3:0] C,
  input  [3:0] Y,
  input  clr_r,
  input  ld_r,
  input  ld_out,
  output [9:0] F
);

  wire ld_c0, ld_c1, ld_c2;
  wire [3:0] rxc_1_ym, rxc_2_ym;
  wire [7:0] adder_1_out, rxc_1_s, rxc_2_s, rxc_3_s;
  wire [8:0] adder_2_out;
  wire [8:8] adder_1_cout;
  wire [9:9] adder_2_cout;

  cod_2x4 cod_2x4_1 (.s_cod1(s_cod0), .s_cod2(s_cod1), .E(en_cod), .s0(ld_c0), .s1(ld_c1), .s2(ld_c2));  // open: s3
  RxC rxc_1 (.C(C), .Y(Y), .ld_r(ld_r), .ld_c(ld_c0), .CLK(CLK), .Ym(rxc_1_ym), .clr_r(clr_r), .S(rxc_1_s));
  RxC rxc_2 (.C(C), .Y(rxc_1_ym), .ld_r(ld_r), .ld_c(ld_c1), .CLK(CLK), .Ym(rxc_2_ym), .clr_r(clr_r), .S(rxc_2_s));
  Adder adder_1 (.a(rxc_2_s), .b(rxc_1_s), .out(adder_1_out), .cout(adder_1_cout[8]));  // open: cin
  RxC rxc_3 (.C(C), .Y(rxc_2_ym), .ld_r(ld_r), .ld_c(ld_c2), .CLK(CLK), .clr_r(clr_r), .S(rxc_3_s));  // open: Ym
  Adder #(.width(9)) adder_2 (
    .a({1'b0, rxc_3_s}), .b({adder_1_cout[8], adder_1_out}), .out(adder_2_out), .cout(adder_2_cout[9]));  // open: cin
  Register #(.width(10), .Select("low")) register_1 (
    .D({adder_2_cout[9], adder_2_out}), .en(ld_out), .Q(F), .clk(CLK));  // open: clr
endmodule
