// Logisim project maqtroco.circ as structural Verilog: 9 circuits, main circuit Main
module Main (
  input  [10:0] in_1
);

  wire aux_1_out_2, aux_1_out_3, aux_1_out_4, aux_1_out_5, aux_1_out_6, aux_1_out_7, aux_1_out_8,
       aux_1_out_9, aux_1_out_10, aux_1_out_11, aux_1_out_12, aux_2_out_2, aux_2_out_3, aux_2_out_4,
       aux_2_out_5, aux_2_out_6, aux_2_out_7, aux_2_out_8, aux_2_out_9, aux_2_out_10, aux_2_out_11,
       aux_2_out_12, aux_3_out_2, aux_3_out_3, aux_3_out_4, aux_3_out_5, aux_3_out_6, aux_3_out_7,
       aux_3_out_8, aux_3_out_9, aux_3_out_10, aux_3_out_11, aux_3_out_12, aux_4_out_2, aux_4_out_3,
       aux_4_out_4, aux_4_out_5, aux_4_out_6, aux_4_out_7, aux_4_out_8, aux_4_out_9, aux_4_out_10,
       aux_4_out_11, aux_4_out_12, aux_5_out_2, aux_5_out_3, aux_5_out_4, aux_5_out_5, aux_5_out_6,
       aux_5_out_7, aux_5_out_8, aux_5_out_9, aux_5_out_10, aux_5_out_11, aux_5_out_12, aux_6_out_2,
       aux_6_out_3, aux_6_out_4, aux_6_out_5, aux_6_out_6, aux_6_out_7, aux_6_out_8, aux_6_out_9,
       aux_6_out_10, aux_6_out_11, aux_6_out_12, bloco_controle_1_clrac, bloco_controle_1_clrt,
       bloco_controle_1_ldt, bloco_controle_1_pisca, bloco_operacional_1_ntt, bloco_operacional_1_tt,
       bloco_operacional_1_tv, CLK, L, Start_out;
  wire [5:0] def;
  wire [10:0] _0_1_COIN, _0_5_COIN, _0_10_COIN, _0_25_COIN, _0_50_COIN, _1_COIN;

  Clock clock_1 (.out(CLK));
  // DipSwitch #(.NSwitches(6)) dipswitch_1: pin names not known
  Aux2 aux2_1 (.out_7(def));  // open: in_1, in_2, in_3, in_4, in_5, in_6
  Button Start (.out(Start_out));
  Bloco_Controle bloco_controle_1 (
    .T(Start_out), .TV(bloco_operacional_1_tv), .TT(bloco_operacional_1_tt), .NTT(bloco_operacional_1_ntt),
    .CLRT(bloco_controle_1_clrt), .CLRAC(bloco_controle_1_clrac), .LDT(bloco_controle_1_ldt),
    .Pisca(bloco_controle_1_pisca), .CLK(CLK));
  Bloco_Operacional bloco_operacional_1 (
    .Pisca(bloco_controle_1_pisca), .LDT(bloco_controle_1_ldt), .CLRT(bloco_controle_1_clrt),
    .CLRAC(bloco_controle_1_clrac), .Banco(def), .in_7(in_1), .out_8(_1_COIN), .out_9(_0_50_COIN),
    .out_10(_0_25_COIN), .out_11(_0_10_COIN), .out_12(_0_5_COIN), .out_13(_0_1_COIN),
    .TT(bloco_operacional_1_tt), .NTT(bloco_operacional_1_ntt), .TV(bloco_operacional_1_tv), .in_2(CLK),
    .out_16(L));
  LED led_1 (.in(aux_1_out_2));
  LED led_2 (.in(aux_1_out_4));
  LED led_3 (.in(aux_1_out_3));
  LED led_4 (.in(aux_1_out_5));
  LED led_5 (.in(aux_2_out_2));
  LED led_6 (.in(aux_2_out_4));
  LED led_7 (.in(aux_2_out_5));
  LED led_8 (.in(aux_2_out_3));
  LED led_9 (.in(aux_3_out_5));
  LED led_10 (.in(aux_3_out_2));
  LED led_11 (.in(aux_3_out_4));
  LED led_12 (.in(aux_3_out_3));
  LED led_13 (.in(aux_4_out_3));
  LED led_14 (.in(aux_4_out_2));
  LED led_15 (.in(aux_4_out_4));
  LED led_16 (.in(aux_4_out_5));
  LED led_17 (.in(aux_5_out_5));
  LED led_18 (.in(aux_5_out_2));
  LED led_19 (.in(aux_5_out_3));
  LED led_20 (.in(aux_5_out_4));
  LED led_21 (.in(aux_6_out_4));
  LED led_22 (.in(aux_6_out_3));
  LED led_23 (.in(aux_6_out_2));
  LED led_24 (.in(aux_6_out_5));
  LED LED_25 (.in(L));
  LED led_26 (.in(aux_1_out_7));
  LED led_27 (.in(aux_1_out_9));
  LED led_28 (.in(aux_1_out_6));
  LED led_29 (.in(aux_1_out_8));
  LED led_30 (.in(aux_2_out_8));
  LED led_31 (.in(aux_2_out_6));
  LED led_32 (.in(aux_2_out_7));
  LED led_33 (.in(aux_2_out_9));
  LED led_34 (.in(aux_3_out_9));
  LED led_35 (.in(aux_3_out_6));
  LED led_36 (.in(aux_3_out_7));
  LED led_37 (.in(aux_3_out_8));
  LED led_38 (.in(aux_4_out_9));
  LED led_39 (.in(aux_4_out_8));
  LED led_40 (.in(aux_4_out_6));
  LED led_41 (.in(aux_4_out_7));
  LED led_42 (.in(aux_5_out_9));
  LED led_43 (.in(aux_5_out_6));
  LED led_44 (.in(aux_5_out_7));
  LED led_45 (.in(aux_5_out_8));
  LED led_46 (.in(aux_6_out_8));
  LED led_47 (.in(aux_6_out_9));
  LED led_48 (.in(aux_6_out_7));
  LED led_49 (.in(aux_6_out_6));
  LED led_50 (.in(aux_1_out_12));
  LED led_51 (.in(aux_1_out_10));
  LED led_52 (.in(aux_1_out_11));
  Aux aux_1 (
    .in_1(_1_COIN), .out_2(aux_1_out_2), .out_3(aux_1_out_3), .out_4(aux_1_out_4), .out_5(aux_1_out_5),
    .out_6(aux_1_out_6), .out_7(aux_1_out_7), .out_8(aux_1_out_8), .out_9(aux_1_out_9),
    .out_10(aux_1_out_10), .out_11(aux_1_out_11), .out_12(aux_1_out_12));
  LED led_53 (.in(aux_2_out_10));
  LED led_54 (.in(aux_2_out_11));
  LED led_55 (.in(aux_2_out_12));
  Aux aux_2 (
    .in_1(_0_50_COIN), .out_2(aux_2_out_2), .out_3(aux_2_out_3), .out_4(aux_2_out_4), .out_5(aux_2_out_5),
    .out_6(aux_2_out_6), .out_7(aux_2_out_7), .out_8(aux_2_out_8), .out_9(aux_2_out_9),
    .out_10(aux_2_out_10), .out_11(aux_2_out_11), .out_12(aux_2_out_12));
  LED led_56 (.in(aux_3_out_12));
  LED led_57 (.in(aux_3_out_10));
  LED led_58 (.in(aux_3_out_11));
  Aux aux_3 (
    .in_1(_0_25_COIN), .out_2(aux_3_out_2), .out_3(aux_3_out_3), .out_4(aux_3_out_4), .out_5(aux_3_out_5),
    .out_6(aux_3_out_6), .out_7(aux_3_out_7), .out_8(aux_3_out_8), .out_9(aux_3_out_9),
    .out_10(aux_3_out_10), .out_11(aux_3_out_11), .out_12(aux_3_out_12));
  LED led_59 (.in(aux_4_out_12));
  LED led_60 (.in(aux_4_out_11));
  LED led_61 (.in(aux_4_out_10));
  Aux aux_4 (
    .in_1(_0_10_COIN), .out_2(aux_4_out_2), .out_3(aux_4_out_3), .out_4(aux_4_out_4), .out_5(aux_4_out_5),
    .out_6(aux_4_out_6), .out_7(aux_4_out_7), .out_8(aux_4_out_8), .out_9(aux_4_out_9),
    .out_10(aux_4_out_10), .out_11(aux_4_out_11), .out_12(aux_4_out_12));
  LED led_62 (.in(aux_5_out_10));
  LED led_63 (.in(aux_5_out_12));
  LED led_64 (.in(aux_5_out_11));
  Aux aux_5 (
    .in_1(_0_5_COIN), .out_2(aux_5_out_2), .out_3(aux_5_out_3), .out_4(aux_5_out_4), .out_5(aux_5_out_5),
    .out_6(aux_5_out_6), .out_7(aux_5_out_7), .out_8(aux_5_out_8), .out_9(aux_5_out_9),
    .out_10(aux_5_out_10), .out_11(aux_5_out_11), .out_12(aux_5_out_12));
  LED led_65 (.in(aux_6_out_12));
  LED led_66 (.in(aux_6_out_10));
  LED led_67 (.in(aux_6_out_11));
  Aux aux_6 (
    .in_1(_0_1_COIN), .out_2(aux_6_out_2), .out_3(aux_6_out_3), .out_4(aux_6_out_4), .out_5(aux_6_out_5),
    .out_6(aux_6_out_6), .out_7(aux_6_out_7), .out_8(aux_6_out_8), .out_9(aux_6_out_9),
    .out_10(aux_6_out_10), .out_11(aux_6_out_11), .out_12(aux_6_out_12));

  // Other names for the same wires on the sheet: V[10:0] = in_1

  // Notes on the sheet:
  //   INPUT:
  //   Definiçao de Moedas:
  //   OUTPUT:
endmodule

module Bloco_Controle (
  input  CLK,
  input  T,
  input  TV,
  input  TT,
  input  NTT,
  output CLRT,
  output CLRAC,
  output LDT,
  output Pisca
);

  wire D0, D1, D2, PRESS, Q0, Q1, Q2;

  BS bs_1 (.T(T), .CLK(CLK), .PRESS(PRESS));
  D_Flip_Flop d_ff_1 (.clk(CLK), .D(D2), .Q(Q2));  // open: Qn, preset, reset
  MLL mll_1 (
    .Q2(Q2), .Q1(Q1), .Q0(Q0), .PRESS(PRESS), .TV(TV), .TT(TT), .NTT(NTT), .D2(D2), .D1(D1), .D0(D0),
    .CLRT(CLRT), .CLRAC(CLRAC), .LDT(LDT), .PIS(Pisca));
  D_Flip_Flop d_ff_2 (.clk(CLK), .D(D1), .Q(Q1));  // open: Qn, preset, reset
  D_Flip_Flop d_ff_3 (.clk(CLK), .D(D0), .Q(Q0));  // open: Qn, preset, reset

  // Notes on the sheet:
  //   BOTAO BS
  //   MAQUINA DE ESTADOS
endmodule

module Bloco_Operacional (
  input  Pisca,
  input  in_2,
  input  LDT,
  input  CLRT,
  input  CLRAC,
  input  [5:0] Banco,
  input  [10:0] in_7,
  output [10:0] out_8,
  output [10:0] out_9,
  output [10:0] out_10,
  output [10:0] out_11,
  output [10:0] out_12,
  output [10:0] out_13,
  output TT,
  output NTT,
  output out_16,
  output TV
);

  wire and_1_out, cond0, cond1, cond2, condicao0, condicao1, condicao2, condicao3, condicao4, condicao5,
       condicao6, j_k_ff_1_q, S0, S1, S2, S3, S4, S5, S6, S7, S8, S9, S10, SOMA1, SOMA5, SOMA10, SOMA25,
       SOMA50, SOMA100;
  wire [10:0] Incrementador, multiplexer_1_out;

  CONDICOES condicoes_1 (
    .SOMA100(SOMA100), .SOMA50(SOMA50), .SOMA25(SOMA25), .SOMA10(SOMA10), .SOMA5(SOMA5), .SOMA1(SOMA1),
    .C1C(Banco[5]), .C2C(Banco[4]), .C3C(Banco[3]), .C4C(Banco[2]), .C5C(Banco[1]), .C6C(Banco[0]),
    .CONDIC0(condicao0), .CONDIC1(condicao1), .CONDIC2(condicao2), .CONDIC3(condicao3), .CONDIC4(condicao4),
    .CONDIC5(condicao5), .CONDIC6(condicao6));
  or or_1 (cond2, condicao4, condicao5, condicao6);
  or or_2 (cond0, condicao1, condicao3, condicao5);
  or or_3 (cond1, condicao2, condicao3, condicao6);
  // SUM_COMP sum_comp_1: pin names not known; wires that end beside it: Incrementador, 11'h64, {S10, S9, S8, S7, S6, S5, S4, S3, S2, S1, S0}, SOMA100
  // SUM_COMP sum_comp_2: pin names not known; wires that end beside it: Incrementador, 11'h32, {S10, S9, S8, S7, S6, S5, S4, S3, S2, S1, S0}, SOMA50
  // SUM_COMP sum_comp_3: pin names not known; wires that end beside it: Incrementador, 11'h19, {S10, S9, S8, S7, S6, S5, S4, S3, S2, S1, S0}, SOMA25
  // SUM_COMP sum_comp_4: pin names not known; wires that end beside it: Incrementador, 11'ha, {S10, S9, S8, S7, S6, S5, S4, S3, S2, S1, S0}, SOMA10
  // SUM_COMP sum_comp_5: pin names not known; wires that end beside it: Incrementador, 11'h5, {S10, S9, S8, S7, S6, S5, S4, S3, S2, S1, S0}, SOMA5
  // SUM_COMP sum_comp_6: pin names not known; wires that end beside it: Incrementador, 11'h1, {S10, S9, S8, S7, S6, S5, S4, S3, S2, S1, S0}, SOMA1
  // REG11Bits reg11bits_1: pin names not known; wires that end beside it: in_7[0], in_7[1], in_7[2], in_7[3], in_7[4], in_7[5], in_7[6], in_7[7], in_7[8], in_7[9], in_7[10], in_2, LDT, CLRT, S0, S1, S2, S3, S4, S5, S6, S7, S8, S9, S10
  and and_1 (and_1_out, ~cond0, cond1, cond2);  // AND_Gate
  // COMP11Bits comp11bits_1: pin names not known; wires that end beside it: TV
  Multiplexer #(.select(3), .width(11), .enable("false")) multiplexer_1 (
    .in0(11'h64), .in1(11'h32), .in2(11'h19), .in3(11'ha), .in4(11'h5), .in5(11'h1), .out(multiplexer_1_out),
    .sel({cond2, cond1, cond0}));  // open: in6, in7
  and and_2 (NTT, and_1_out, ~TT);  // AND_Gate
  // SUM_REG sum_reg_1: pin names not known; wires that end beside it: multiplexer_1_out, in_2, CLRAC, 1'b1, Incrementador
  // COMP11Bits comp11bits_2: pin names not known; wires that end beside it: TT
  ACUMULADOR_COIN acumulador_coin_1 (.COND(condicao0), .CLK(in_2), .CLR(CLRAC), .out_4(out_8));
  ACUMULADOR_COIN acumulador_coin_2 (.COND(condicao1), .CLK(in_2), .CLR(CLRAC), .out_4(out_9));
  ACUMULADOR_COIN acumulador_coin_3 (.COND(condicao2), .CLK(in_2), .CLR(CLRAC), .out_4(out_10));
  ACUMULADOR_COIN acumulador_coin_4 (.COND(condicao3), .CLK(in_2), .CLR(CLRAC), .out_4(out_11));
  ACUMULADOR_COIN acumulador_coin_5 (.COND(condicao4), .CLK(in_2), .CLR(CLRAC), .out_4(out_12));
  ACUMULADOR_COIN acumulador_coin_6 (.COND(condicao5), .CLK(in_2), .CLR(CLRAC), .out_4(out_13));
  J_K_Flip_Flop j_k_ff_1 (.J(Pisca), .clk(in_2), .K(Pisca), .Q(j_k_ff_1_q));  // open: Qn, preset, reset
  Multiplexer #(.enable("false")) multiplexer_2 (.in0(1'b1), .in1(j_k_ff_1_q), .out(out_16), .sel(Pisca));

  // Other names for the same wires on the sheet: TC1 = Banco[0]; TC5 = Banco[1]; TC10 = Banco[2]; TC25 = Banco[3];
  //   TC50 = Banco[4]; TC100 = Banco[5]; CLK = in_2; clr_acumulador = CLRAC; clr_troco = CLRT; A0 = in_7[0];
  //   A1 = in_7[1]; A2 = in_7[2]; A3 = in_7[3]; A4 = in_7[4]; A5 = in_7[5]; A6 = in_7[6]; A7 = in_7[7]; A8 = in_7[8];
  //   A9 = in_7[9]; A10 = in_7[10]; L = out_16; ld_troco = LDT; libera1[10:0] = out_8; libera2[10:0] = out_9;
  //   libera3[10:0] = out_10; libera4[10:0] = out_11; libera5[10:0] = out_12; libera6[10:0] = out_13;
  //   NaoTemTroco = NTT; SelCond[2:0] = {cond2, cond1, cond0}; TemTroco = TT; TemValor = TV;
  //   V11BITS[10:0] = {S10, S9, S8, S7, S6, S5, S4, S3, S2, S1, S0}

  // Notes on the sheet:
  //   VALOR
  //   ENTRADAS
  //   CONDIÇÕES
  //   COFRES
  //   PROCESSATROCO
  //   1R
  //   50C
  //   25C
  //   10C
  //   5C
  //   1C
  //   ACUMULADOR
  //   SAIDA L
endmodule

module MLL (
  input  Q2,
  input  Q1,
  input  Q0,
  input  PRESS,
  input  TV,
  input  TT,
  input  NTT,
  output D2,
  output D1,
  output D0,
  output CLRT,
  output CLRAC,
  output LDT,
  output PIS
);

  wire and_2_out, and_3_out, and_4_out, and_5_out, and_6_out, and_7_out, and_8_out, and_9_out, and_11_out,
       and_12_out, and_13_out, not_1_out, not_2_out, not_3_out, not_4_out, not_5_out, not_6_out, not_7_out,
       not_8_out, not_9_out, not_10_out, not_11_out, not_12_out, not_13_out, not_14_out, not_15_out,
       not_16_out, not_17_out, not_18_out, not_19_out, not_20_out, not_21_out, not_22_out, not_23_out,
       not_24_out, not_25_out, not_26_out, not_27_out, not_28_out, not_29_out, not_30_out;

  not not_1 (not_1_out, Q2);
  not not_2 (not_2_out, Q0);
  not not_3 (not_3_out, NTT);
  not not_4 (not_4_out, Q2);
  not not_5 (not_5_out, Q1);
  not not_6 (not_6_out, Q2);
  not not_7 (not_7_out, Q0);
  not not_8 (not_8_out, TT);
  not not_9 (not_9_out, Q2);
  not not_10 (not_10_out, Q1);
  not not_11 (not_11_out, Q0);
  not not_12 (not_12_out, Q2);
  not not_13 (not_13_out, Q0);
  not not_14 (not_14_out, TT);
  not not_15 (not_15_out, Q2);
  not not_16 (not_16_out, Q1);
  not not_17 (not_17_out, Q0);
  not not_18 (not_18_out, Q2);
  not not_19 (not_19_out, Q1);
  not not_20 (not_20_out, Q2);
  not not_21 (not_21_out, Q2);
  not not_22 (not_22_out, Q1);
  not not_23 (not_23_out, Q2);
  not not_24 (not_24_out, Q1);
  not not_25 (not_25_out, Q2);
  not not_26 (not_26_out, Q0);
  not not_27 (not_27_out, TT);
  not not_28 (not_28_out, Q2);
  not not_29 (not_29_out, Q0);
  not not_30 (not_30_out, NTT);
  and and_1 (D2, not_1_out, Q1, not_2_out, TT, not_3_out);
  and and_2 (and_2_out, not_4_out, not_5_out, Q0);
  and and_3 (and_3_out, not_6_out, Q1, not_7_out, not_8_out);
  and and_4 (and_4_out, not_9_out, not_10_out, not_11_out, PRESS, TV);
  and and_5 (and_5_out, not_12_out, Q1, not_13_out, not_14_out, NTT);
  and and_6 (and_6_out, not_15_out, Q1, Q0);
  and and_7 (and_7_out, Q2, not_16_out, not_17_out);
  and and_8 (and_8_out, not_18_out, not_19_out, Q0);
  and and_9 (and_9_out, not_20_out, Q1, Q0);
  and and_10 (LDT, not_21_out, not_22_out, Q0);
  and and_11 (and_11_out, not_23_out, not_24_out, Q0);
  and and_12 (and_12_out, not_25_out, Q1, not_26_out, not_27_out);
  and and_13 (and_13_out, not_28_out, Q1, not_29_out, not_30_out);
  or or_1 (D1, and_2_out, and_3_out);
  or or_2 (D0, and_4_out, and_5_out);
  or or_3 (CLRT, and_6_out, and_7_out);
  or or_4 (CLRAC, and_8_out, and_9_out);
  or or_5 (PIS, and_11_out, and_12_out, and_13_out);
endmodule

module CONDICOES (
  input  SOMA100,
  input  SOMA50,
  input  SOMA25,
  input  SOMA10,
  input  SOMA5,
  input  SOMA1,
  input  C1C,
  input  C2C,
  input  C3C,
  input  C4C,
  input  C5C,
  input  C6C,
  output CONDIC0,
  output CONDIC1,
  output CONDIC2,
  output CONDIC3,
  output CONDIC4,
  output CONDIC5,
  output CONDIC6
);

  wire and_2_out, and_4_out, and_5_out, and_6_out, and_7_out, and_8_out, and_9_out, and_10_out, and_11_out,
       and_12_out, and_13_out, and_15_out, and_16_out, and_17_out, and_18_out, and_19_out, and_20_out,
       and_21_out, and_22_out, not_1_out, not_2_out, not_3_out, not_4_out, not_5_out, not_6_out, not_7_out,
       not_8_out, not_9_out, not_10_out, not_11_out, not_12_out, not_13_out, not_14_out, not_15_out,
       not_16_out, not_17_out, not_18_out, not_19_out, not_20_out, not_21_out, not_22_out, not_23_out,
       not_24_out, not_25_out, not_26_out, not_27_out, or_1_out, or_2_out, or_3_out, or_4_out, or_5_out,
       or_6_out, or_7_out, or_8_out, or_9_out, or_10_out, or_11_out, or_12_out, or_13_out, or_14_out,
       or_15_out, or_16_out, or_17_out, or_18_out, or_19_out, or_20_out, or_21_out;

  not not_1 (not_1_out, SOMA100);
  and and_1 (CONDIC0, not_1_out, C1C);
  not not_2 (not_2_out, SOMA50);
  and and_2 (and_2_out, not_2_out, C2C);
  or or_1 (or_1_out, SOMA100, not_3_out);
  not not_3 (not_3_out, C1C);
  or or_2 (or_2_out, SOMA100, not_4_out);
  not not_4 (not_4_out, C1C);
  or or_3 (or_3_out, SOMA50, not_5_out);
  not not_5 (not_5_out, C2C);
  not not_6 (not_6_out, SOMA25);
  or or_4 (or_4_out, SOMA100, not_7_out);
  not not_7 (not_7_out, C1C);
  or or_5 (or_5_out, SOMA50, not_8_out);
  not not_8 (not_8_out, C2C);
  not not_9 (not_9_out, C3C);
  or or_6 (or_6_out, SOMA100, not_10_out);
  not not_10 (not_10_out, C1C);
  or or_7 (or_7_out, SOMA50, not_11_out);
  not not_11 (not_11_out, C2C);
  not not_12 (not_12_out, C3C);
  or or_8 (or_8_out, SOMA10, not_13_out);
  not not_13 (not_13_out, C4C);
  not not_14 (not_14_out, SOMA5);
  or or_9 (or_9_out, SOMA100, not_15_out);
  not not_15 (not_15_out, C1C);
  or or_10 (or_10_out, SOMA50, not_16_out);
  not not_16 (not_16_out, C2C);
  or or_11 (or_11_out, SOMA25, not_17_out);
  not not_17 (not_17_out, C3C);
  or or_12 (or_12_out, SOMA10, not_18_out);
  not not_18 (not_18_out, C4C);
  or or_13 (or_13_out, SOMA5, not_19_out);
  not not_19 (not_19_out, C5C);
  not not_20 (not_20_out, SOMA1);
  or or_14 (or_14_out, SOMA100, not_21_out);
  not not_21 (not_21_out, C1C);
  or or_15 (or_15_out, SOMA50, not_22_out);
  not not_22 (not_22_out, C2C);
  not not_23 (not_23_out, C3C);
  or or_16 (or_16_out, SOMA10, not_24_out);
  not not_24 (not_24_out, C4C);
  or or_17 (or_17_out, SOMA5, not_25_out);
  not not_25 (not_25_out, C5C);
  not not_26 (not_26_out, C6C);
  and and_3 (CONDIC1, and_2_out, or_1_out);
  and and_4 (and_4_out, or_2_out, or_3_out);
  and and_5 (and_5_out, not_6_out, C3C);
  and and_6 (and_6_out, or_4_out, or_5_out);
  or or_18 (or_18_out, SOMA25, not_9_out);
  not not_27 (not_27_out, SOMA10);
  and and_7 (and_7_out, or_6_out, or_7_out);
  or or_19 (or_19_out, SOMA25, not_12_out);
  and and_8 (and_8_out, or_8_out, not_14_out);
  and and_9 (and_9_out, or_9_out, or_10_out);
  and and_10 (and_10_out, or_11_out, or_12_out);
  and and_11 (and_11_out, or_13_out, not_20_out);
  and and_12 (and_12_out, or_14_out, or_15_out);
  or or_20 (or_20_out, SOMA25, not_23_out);
  and and_13 (and_13_out, or_16_out, or_17_out);
  or or_21 (or_21_out, SOMA1, not_26_out);
  and and_14 (CONDIC2, and_4_out, and_5_out);
  and and_15 (and_15_out, and_6_out, or_18_out);
  and and_16 (and_16_out, not_27_out, C4C);
  and and_17 (and_17_out, and_7_out, or_19_out);
  and and_18 (and_18_out, and_8_out, C5C);
  and and_19 (and_19_out, and_9_out, and_10_out);
  and and_20 (and_20_out, and_11_out, C6C);
  and and_21 (and_21_out, and_12_out, or_20_out);
  and and_22 (and_22_out, and_13_out, or_21_out);
  and and_23 (CONDIC3, and_15_out, and_16_out);
  and and_24 (CONDIC4, and_17_out, and_18_out);
  and and_25 (CONDIC5, and_19_out, and_20_out);
  and and_26 (CONDIC6, and_21_out, and_22_out);
endmodule

module ACUMULADOR_COIN (
  input  COND,
  input  CLK,
  input  CLR,
  output [10:0] out_4
);

  wire [10:10] not_1_out;

  not not_1 (not_1_out[10], COND);
  Counter #(.width(11), .max('h7ff)) counter_1 (
    .D({11{not_1_out[10]}}), .count(COND), .Q(out_4), .clk(CLK), .clr(CLR));  // open: load, carry, preset, down
endmodule

module BS (
  input  T,
  input  CLK,
  output PRESS
);

  wire button_1_p1, button_1_p2, button_1_p4, button_1_p5;

  // Digital_Oscilloscope #(.nState(20)) digital_oscilloscope_1: pin names not known; wires that end beside it: CLK, PRESS, 1'b1
  // Button button_1: pin names not known; wires that end beside it: button_1_p1, button_1_p2, T, button_1_p4, button_1_p5, PRESS
  D_Flip_Flop d_ff_1 (.clk(CLK), .D(button_1_p4), .Q(button_1_p1));  // open: Qn, preset, reset
  D_Flip_Flop d_ff_2 (.clk(CLK), .D(button_1_p5), .Q(button_1_p2));  // open: Qn, preset, reset

  // Notes on the sheet:
  //   BOTAO BS
endmodule

module Aux (
  input  [10:0] in_1,
  output out_2,
  output out_3,
  output out_4,
  output out_5,
  output out_6,
  output out_7,
  output out_8,
  output out_9,
  output out_10,
  output out_11,
  output out_12
);


  assign out_2 = in_1[10];
  assign out_3 = in_1[9];
  assign out_4 = in_1[8];
  assign out_5 = in_1[7];
  assign out_6 = in_1[6];
  assign out_7 = in_1[5];
  assign out_8 = in_1[4];
  assign out_9 = in_1[3];
  assign out_10 = in_1[2];
  assign out_11 = in_1[1];
  assign out_12 = in_1[0];
endmodule

module Aux2 (
  input  in_1,
  input  in_2,
  input  in_3,
  input  in_4,
  input  in_5,
  input  in_6,
  output [5:0] out_7
);


  assign out_7 = {in_1, in_2, in_3, in_4, in_5, in_6};
endmodule
