// Logisim project fifo21.circ as structural Verilog: 4 circuits, main circuit main
module main (
  input  [12:0] in_1,
  input  in_2,
  input  [3:0] in_3,
  input  [3:0] in_4,
  output [3:0] out_5,
  output [3:0] out_6,
  output [12:0] out_7,
  output [12:0] out_8,
  output [12:0] out_9,
  output [12:0] out_10,
  output [12:0] out_11,
  output [12:0] out_12,
  output [12:0] out_13,
  output [12:0] out_14,
  output [12:0] out_15,
  output [12:0] out_16,
  output [12:0] out_17,
  output [12:0] out_18,
  output [12:0] out_19,
  output [12:0] out_20,
  output [12:0] out_21,
  output [12:0] out_22,
  output [12:0] out_23,
  output [12:0] out_24
);

  wire button_1_out, button_2_out, clk, clr1, clr2, clr3, clr4, clr5, clr6, clr7, clr8, clr9, clr10, clr11,
       clr12, clr13, clr14, clr15, clr16, CLR_REG, clr_reg1, clr_reg2, clr_reg3, clr_reg4, clr_reg5,
       clr_reg6, clr_reg7, clr_reg8, clr_reg9, clr_reg10, clr_reg11, clr_reg12, clr_reg13, clr_reg14,
       clr_reg15, clr_reg16, CONT_1, CONT_2, EMP, en_reg1, en_reg2, en_reg3, en_reg4, en_reg5, en_reg6,
       en_reg7, en_reg8, en_reg9, en_reg10, en_reg11, en_reg12, en_reg13, en_reg14, en_reg15, en_reg16,
       ESCREVA, FU, LEIA, RD, reg1, reg2, reg3, reg4, reg5, reg6, reg7, reg8, reg9, reg10, reg11, reg12,
       reg13, reg14, reg15, reg16, WR;

  Demultiplexer #(.select(4), .enable("false")) demultiplexer_1 (
    .out0(en_reg1), .out1(en_reg2), .out2(en_reg3), .out3(en_reg4), .out4(en_reg5), .out5(en_reg6),
    .out6(en_reg7), .out7(en_reg8), .out8(en_reg9), .out9(en_reg10), .out10(en_reg11), .out11(en_reg12),
    .out12(en_reg13), .out13(en_reg14), .out14(en_reg15), .out15(en_reg16), .in(ESCREVA), .sel(out_5));
  Register #(.width(14), .Select("low")) register_1 (
    .D({en_reg1, in_1}), .en(en_reg1), .Q({reg1, out_9}), .clk(clk), .clr(clr_reg1));
  Register #(.width(14), .Select("low")) register_2 (
    .D({en_reg5, in_1}), .en(en_reg5), .Q({reg5, out_17}), .clk(clk), .clr(clr_reg5));
  Register #(.width(14), .Select("low")) register_3 (
    .D({en_reg9, in_1}), .en(en_reg9), .Q({reg9, out_24}), .clk(clk), .clr(clr_reg9));
  Register #(.width(14), .Select("low")) register_4 (
    .D({en_reg13, in_1}), .en(en_reg13), .Q({reg13, out_16}), .clk(clk), .clr(clr_reg13));
  and and_1 (FU, reg1, reg2, reg3, reg4, reg5, reg6, reg7, reg8, reg9, reg10, reg11, reg12, reg13, reg14, reg15, reg16);
  and and_2 (EMP, ~reg1, ~reg2, ~reg3, ~reg4, ~reg5, ~reg6, ~reg7, ~reg8, ~reg9, ~reg10, ~reg11, ~reg12, ~reg13, ~reg14, ~reg15, ~reg16);  // AND_Gate
  Demultiplexer #(.select(4), .enable("false")) demultiplexer_2 (
    .out0(clr1), .out1(clr2), .out2(clr3), .out3(clr4), .out4(clr5), .out5(clr6), .out6(clr7), .out7(clr8),
    .out8(clr9), .out9(clr10), .out10(clr11), .out11(clr12), .out12(clr13), .out13(clr14), .out14(clr15),
    .out15(clr16), .in(CLR_REG), .sel(out_6));
  Register #(.width(14), .Select("low")) register_5 (
    .D({en_reg2, in_1}), .en(en_reg2), .Q({reg2, out_11}), .clk(clk), .clr(clr_reg2));
  Register #(.width(14), .Select("low")) register_6 (
    .D({en_reg6, in_1}), .en(en_reg6), .Q({reg6, out_19}), .clk(clk), .clr(clr_reg6));
  Register #(.width(14), .Select("low")) register_7 (
    .D({en_reg10, in_1}), .en(en_reg10), .Q({reg10, out_10}), .clk(clk), .clr(clr_reg10));
  Register #(.width(14), .Select("low")) register_8 (
    .D({en_reg14, in_1}), .en(en_reg14), .Q({reg14, out_18}), .clk(clk), .clr(clr_reg14));
  Clock clock_1 (.out(clk));
  BLOCO_DE_CONTROLE bloco_de_controle_1 (
    .WR(WR), .RD(RD), .FU(FU), .EM(EMP), .CLK(clk), .CLR_FIFO(in_2), .CONT_1(CONT_1), .CONT_2(CONT_2),
    .CLR_REG(CLR_REG), .LEIA(LEIA), .ESCREVA(ESCREVA));
  Button button_1 (.out(button_1_out));
  Button button_2 (.out(button_2_out));
  BS bs_1 (.T(button_1_out), .CLK(clk), .S(RD));
  BS bs_2 (.T(button_2_out), .CLK(clk), .S(WR));
  or or_1 (clr_reg1, in_2, clr1);
  or or_2 (clr_reg2, in_2, clr2);
  or or_3 (clr_reg3, in_2, clr3);
  or or_4 (clr_reg4, in_2, clr4);
  or or_5 (clr_reg5, in_2, clr5);
  or or_6 (clr_reg6, in_2, clr6);
  or or_7 (clr_reg7, in_2, clr7);
  or or_8 (clr_reg8, in_2, clr8);
  or or_9 (clr_reg9, in_2, clr9);
  or or_10 (clr_reg10, in_2, clr10);
  or or_11 (clr_reg11, in_2, clr11);
  or or_12 (clr_reg12, in_2, clr12);
  or or_13 (clr_reg13, in_2, clr13);
  or or_14 (clr_reg14, in_2, clr14);
  or or_15 (clr_reg15, in_2, clr15);
  or or_16 (clr_reg16, in_2, clr16);
  Register #(.width(14), .Select("low")) register_9 (
    .D({en_reg3, in_1}), .en(en_reg3), .Q({reg3, out_13}), .clk(clk), .clr(clr_reg3));
  Register #(.width(14), .Select("low")) register_10 (
    .D({en_reg7, in_1}), .en(en_reg7), .Q({reg7, out_21}), .clk(clk), .clr(clr_reg7));
  Register #(.width(14), .Select("low")) register_11 (
    .D({en_reg11, in_1}), .en(en_reg11), .Q({reg11, out_12}), .clk(clk), .clr(clr_reg11));
  Register #(.width(14), .Select("low")) register_12 (
    .D({en_reg15, in_1}), .en(en_reg15), .Q({reg15, out_20}), .clk(clk), .clr(clr_reg15));
  Counter #(.width(4), .max('hf)) counter_1 (
    .D(in_3), .count(CONT_1), .Q(out_5), .clk(clk), .clr(in_2));  // open: load, carry, preset, down
  Counter #(.width(4), .max('hf)) counter_2 (
    .D(in_4), .count(CONT_2), .Q(out_6), .clk(clk), .clr(in_2));  // open: load, carry, preset, down
  Register #(.width(14), .Select("low")) register_13 (
    .D({en_reg4, in_1}), .en(en_reg4), .Q({reg4, out_15}), .clk(clk), .clr(clr_reg4));
  Register #(.width(14), .Select("low")) register_14 (
    .D({en_reg8, in_1}), .en(en_reg8), .Q({reg8, out_23}), .clk(clk), .clr(clr_reg8));
  Register #(.width(14), .Select("low")) register_15 (
    .D({en_reg12, in_1}), .en(en_reg12), .Q({reg12, out_14}), .clk(clk), .clr(clr_reg12));
  Register #(.width(14), .Select("low")) register_16 (
    .D({en_reg16, in_1}), .en(en_reg16), .Q({reg16, out_22}), .clk(clk), .clr(clr_reg16));
  Multiplexer #(.select(4), .width(13), .enable("false")) multiplexer_1 (
    .in0(out_9), .in1(out_11), .in2(out_13), .in3(out_15), .in4(out_17), .in5(out_19), .in6(out_21),
    .in7(out_23), .in8(out_24), .in9(out_10), .in10(out_12), .in11(out_14), .in12(out_16), .in13(out_18),
    .in14(out_20), .in15(out_22), .out(out_8), .sel(out_6));
  Register #(.width(13), .Select("low")) register_17 (.D(out_8), .en(RD), .Q(out_7), .clk(clk));  // open: clr

  // Other names for the same wires on the sheet: input[12:0] = in_1; ADRESS1[3:0] = out_5; ADRESS2[3:0] = out_6;
  //   CLR_FIFO = in_2; output1[12:0] = out_9; output2[12:0] = out_11; output3[12:0] = out_13; output4[12:0] = out_15;
  //   output5[12:0] = out_17; output6[12:0] = out_19; output7[12:0] = out_21; output8[12:0] = out_23;
  //   output9[12:0] = out_24; output10[12:0] = out_10; output11[12:0] = out_12; output12[12:0] = out_14;
  //   output13[12:0] = out_16; output14[12:0] = out_18; output15[12:0] = out_20; output16[12:0] = out_22;
  //   output_fifo[12:0] = out_8
endmodule

module LOG_COMB (
  input  Q2,
  input  Q1,
  input  Q0,
  input  WR,
  input  RD,
  input  FU,
  input  EM,
  output D2,
  output D1,
  output D0,
  output CONT_1,
  output CONT_2,
  output CLR_REG,
  output LEIA,
  output ESCREVA
);

  wire and_2_out, and_3_out, and_4_out, and_5_out, and_6_out, and_7_out, and_8_out, and_9_out, and_10_out,
       and_11_out, and_12_out, and_13_out, and_14_out, and_15_out, and_16_out, and_17_out, and_18_out,
       and_19_out, and_20_out, and_21_out, and_22_out, and_23_out, and_24_out, and_25_out, and_26_out,
       and_27_out, and_28_out, and_29_out, and_33_out, and_34_out, and_35_out, and_36_out, not_1_out,
       not_2_out, not_3_out, not_4_out, not_5_out, not_6_out, not_7_out, not_8_out, not_9_out, not_10_out,
       not_11_out, not_12_out, not_13_out, not_14_out, not_15_out, not_16_out, not_17_out, not_18_out,
       not_19_out, not_20_out, not_21_out, not_22_out, not_23_out, not_24_out, not_25_out, or_1_out,
       or_2_out, or_3_out, or_4_out, or_5_out, or_7_out, or_9_out, or_10_out;

  not not_1 (not_1_out, Q2);
  not not_2 (not_2_out, WR);
  not not_3 (not_3_out, WR);
  not not_4 (not_4_out, RD);
  not not_5 (not_5_out, EM);
  not not_6 (not_6_out, Q2);
  not not_7 (not_7_out, Q1);
  not not_8 (not_8_out, RD);
  not not_9 (not_9_out, Q2);
  and and_1 (CONT_2, Q2, Q1);
  not not_10 (not_10_out, Q1);
  not not_11 (not_11_out, Q1);
  not not_12 (not_12_out, Q2);
  not not_13 (not_13_out, Q1);
  not not_14 (not_14_out, Q1);
  and and_2 (and_2_out, not_1_out, Q1);
  and and_3 (and_3_out, not_2_out, RD);
  not not_15 (not_15_out, EM);
  not not_16 (not_16_out, Q1);
  not not_17 (not_17_out, Q0);
  and and_4 (and_4_out, Q1, not_3_out);
  and and_5 (and_5_out, not_4_out, not_5_out);
  not not_18 (not_18_out, Q0);
  and and_6 (and_6_out, not_6_out, not_7_out);
  and and_7 (and_7_out, Q0, FU);
  not not_19 (not_19_out, Q0);
  and and_8 (and_8_out, Q1, not_8_out);
  not not_20 (not_20_out, EM);
  and and_9 (and_9_out, Q1, WR);
  not not_21 (not_21_out, EM);
  not not_22 (not_22_out, Q0);
  and and_10 (and_10_out, not_9_out, Q1);
  not not_23 (not_23_out, Q0);
  and and_11 (and_11_out, Q2, Q1);
  and and_12 (and_12_out, Q2, not_10_out);
  and and_13 (and_13_out, Q2, not_11_out);
  not not_24 (not_24_out, Q0);
  and and_14 (and_14_out, not_12_out, not_13_out);
  and and_15 (and_15_out, not_14_out, Q0);
  and and_16 (and_16_out, and_2_out, Q0);
  and and_17 (and_17_out, and_3_out, not_15_out);
  and and_18 (and_18_out, not_16_out, Q0);
  and and_19 (and_19_out, Q1, not_17_out);
  and and_20 (and_20_out, and_4_out, and_5_out);
  and and_21 (and_21_out, Q2, Q1);
  and and_22 (and_22_out, not_18_out, WR);
  and and_23 (and_23_out, and_6_out, and_7_out);
  and and_24 (and_24_out, Q1, not_19_out);
  and and_25 (and_25_out, and_8_out, not_20_out);
  and and_26 (and_26_out, and_9_out, not_21_out);
  and and_27 (and_27_out, Q2, not_22_out);
  and and_28 (and_28_out, and_10_out, not_23_out);
  and and_29 (and_29_out, and_11_out, Q0);
  and and_30 (CLR_REG, and_12_out, Q0);
  and and_31 (LEIA, and_13_out, not_24_out);
  and and_32 (ESCREVA, and_14_out, Q0);
  and and_33 (and_33_out, and_15_out, FU);
  and and_34 (and_34_out, and_16_out, and_17_out);
  not not_25 (not_25_out, Q1);
  or or_1 (or_1_out, and_18_out, and_19_out);
  or or_2 (or_2_out, and_20_out, and_21_out);
  or or_3 (or_3_out, and_22_out, and_23_out);
  or or_4 (or_4_out, and_24_out, and_25_out);
  or or_5 (or_5_out, and_26_out, and_27_out);
  and and_35 (and_35_out, Q2, Q1);
  or or_6 (CONT_1, and_28_out, and_29_out);
  or or_7 (or_7_out, and_33_out, and_34_out);
  and and_36 (and_36_out, Q2, not_25_out);
  or or_8 (D1, or_1_out, or_2_out);
  or or_9 (or_9_out, or_3_out, or_4_out);
  or or_10 (or_10_out, or_5_out, and_35_out);
  or or_11 (D2, or_7_out, and_36_out);
  or or_12 (D0, or_9_out, or_10_out);
endmodule

module BLOCO_DE_CONTROLE (
  input  CLK,
  input  CLR_FIFO,
  input  WR,
  input  RD,
  input  FU,
  input  EM,
  output CONT_1,
  output CONT_2,
  output CLR_REG,
  output LEIA,
  output ESCREVA
);

  wire [2:0] log_comb_1_d0, register_1_q;

  LOG_COMB log_comb_1 (
    .Q2(register_1_q[2]), .Q1(register_1_q[1]), .Q0(register_1_q[0]), .WR(WR), .RD(RD), .FU(FU), .EM(EM),
    .D2(log_comb_1_d0[2]), .D1(log_comb_1_d0[1]), .D0(log_comb_1_d0[0]), .CONT_1(CONT_1), .CONT_2(CONT_2),
    .CLR_REG(CLR_REG), .LEIA(LEIA), .ESCREVA(ESCREVA));
  Register #(.width(3), .Select("low")) register_1 (
    .D(log_comb_1_d0), .Q(register_1_q), .clk(CLK), .clr(CLR_FIFO));  // open: en

  // Other names for the same wires on the sheet: CLR = CLR_FIFO
endmodule

module BS (
  input  T,
  input  CLK,
  output S
);

  wire and_1_out, and_2_out, and_4_out, and_5_out, D0, D1, not_1_out, not_2_out, not_3_out, not_4_out,
       not_5_out, Q0, Q1;

  not not_1 (not_1_out, Q0);
  not not_2 (not_2_out, Q1);
  not not_3 (not_3_out, Q0);
  not not_4 (not_4_out, Q1);
  not not_5 (not_5_out, Q1);
  and and_1 (and_1_out, Q1, not_1_out);
  and and_2 (and_2_out, not_2_out, not_3_out);
  and and_3 (S, not_4_out, Q0);
  and and_4 (and_4_out, not_5_out, Q0);
  and and_5 (and_5_out, and_1_out, T);
  and and_6 (D0, and_2_out, T);
  Register #(.width(2), .Select("low")) register_1 (.D({D1, D0}), .Q({Q1, Q0}), .clk(CLK));  // open: en, clr
  or or_1 (D1, and_4_out, and_5_out);
endmodule
