// Logisim project TEO11.circ as structural Verilog: 6 circuits, main circuit main
module main (
  input  [3:0] in_1,
  input  CLRB,
  input  RDB,
  input  WRB,
  output [3:0] out_5,
  output [3:0] out_6,
  output [3:0] out_7
);

  wire bloco_de_controle_1_clr, bloco_de_controle_1_rd, bloco_de_controle_1_wr, bloco_operacional_1_em,
       bloco_operacional_1_fu, clock_1_out;

  Clock clock_1 (.out(clock_1_out));
  BLOCO_DE_CONTROLE bloco_de_controle_1 (
    .EM(bloco_operacional_1_em), .FU(bloco_operacional_1_fu), .CLR(bloco_de_controle_1_clr),
    .RD(bloco_de_controle_1_rd), .WR(bloco_de_controle_1_wr), .in_6(clock_1_out), .RDB(RDB), .WRB(WRB),
    .CLRB(CLRB));
  BLOCO_OPERACIONAL bloco_operacional_1 (
    .WR(bloco_de_controle_1_wr), .RD(bloco_de_controle_1_rd), .CLR(bloco_de_controle_1_clr),
    .CLK(clock_1_out), .valor(in_1), .WRVA(out_5), .RDVA(out_6), .svalor(out_7), .EM(bloco_operacional_1_em),
    .FU(bloco_operacional_1_fu));
endmodule

module MLL (
  input  Q1,
  input  Q0,
  input  CLR_B,
  input  CLRMAX,
  input  RD_B,
  input  WR_B,
  input  EM,
  input  FU,
  output D1,
  output D0,
  output CLR,
  output RD,
  output WR
);

  wire and_2_out, and_3_out, and_4_out, and_5_out, and_6_out, and_7_out, and_9_out, and_10_out, and_11_out,
       and_12_out, and_13_out, and_14_out, and_15_out, and_16_out, and_17_out, and_18_out, and_19_out,
       and_20_out, and_21_out, and_22_out, not_1_out, not_2_out, not_3_out, not_4_out, not_5_out, not_6_out,
       not_7_out, not_8_out, not_9_out, not_10_out, not_11_out, not_12_out, not_13_out, not_14_out,
       not_15_out, not_16_out, not_17_out, not_18_out, not_19_out, not_20_out, not_21_out, not_22_out,
       not_23_out, not_24_out, not_25_out, not_26_out, not_27_out, not_28_out, not_29_out, not_30_out,
       not_31_out, not_32_out, not_33_out, not_34_out, not_35_out, not_36_out, not_37_out, not_38_out,
       not_39_out, not_40_out, not_41_out, not_42_out, not_43_out, not_44_out, not_45_out, not_46_out,
       not_47_out, not_48_out, not_49_out, not_50_out, not_51_out, not_52_out, not_53_out, not_54_out,
       not_55_out, not_56_out, not_57_out, not_58_out, not_59_out;

  not not_1 (not_1_out, Q1);
  not not_2 (not_2_out, Q0);
  not not_3 (not_3_out, CLR_B);
  not not_4 (not_4_out, CLRMAX);
  not not_5 (not_5_out, Q1);
  not not_6 (not_6_out, Q0);
  not not_7 (not_7_out, CLR_B);
  not not_8 (not_8_out, RD_B);
  not not_9 (not_9_out, Q1);
  not not_10 (not_10_out, Q0);
  not not_11 (not_11_out, CLR_B);
  not not_12 (not_12_out, WR_B);
  not not_13 (not_13_out, Q1);
  not not_14 (not_14_out, Q0);
  not not_15 (not_15_out, CLR_B);
  not not_16 (not_16_out, EM);
  not not_17 (not_17_out, Q1);
  not not_18 (not_18_out, Q0);
  not not_19 (not_19_out, CLR_B);
  not not_20 (not_20_out, FU);
  not not_21 (not_21_out, Q1);
  not not_22 (not_22_out, Q0);
  not not_23 (not_23_out, WR_B);
  not not_24 (not_24_out, EM);
  not not_25 (not_25_out, Q1);
  not not_26 (not_26_out, Q0);
  not not_27 (not_27_out, Q1);
  not not_28 (not_28_out, Q0);
  not not_29 (not_29_out, CLR_B);
  not not_30 (not_30_out, CLRMAX);
  not not_31 (not_31_out, Q1);
  not not_32 (not_32_out, Q0);
  not not_33 (not_33_out, CLR_B);
  not not_34 (not_34_out, RD_B);
  not not_35 (not_35_out, Q1);
  not not_36 (not_36_out, Q0);
  not not_37 (not_37_out, CLR_B);
  not not_38 (not_38_out, WR_B);
  not not_39 (not_39_out, Q1);
  not not_40 (not_40_out, Q0);
  not not_41 (not_41_out, CLR_B);
  not not_42 (not_42_out, EM);
  not not_43 (not_43_out, Q1);
  not not_44 (not_44_out, Q0);
  not not_45 (not_45_out, CLR_B);
  not not_46 (not_46_out, FU);
  not not_47 (not_47_out, Q1);
  not not_48 (not_48_out, Q0);
  not not_49 (not_49_out, RD_B);
  not not_50 (not_50_out, FU);
  not not_51 (not_51_out, Q1);
  not not_52 (not_52_out, Q0);
  and and_1 (CLR, Q1, Q0);
  and and_2 (and_2_out, Q1, not_53_out, FU);
  not not_53 (not_53_out, Q0);
  not not_54 (not_54_out, Q0);
  and and_3 (and_3_out, Q1, not_54_out, EM);
  not not_55 (not_55_out, Q0);
  and and_4 (and_4_out, Q1, not_55_out, WR_B);
  and and_5 (and_5_out, Q1, not_56_out, RD_B);
  not not_56 (not_56_out, Q0);
  not not_57 (not_57_out, Q0);
  and and_6 (and_6_out, Q1, not_57_out, CLRMAX);
  not not_58 (not_58_out, Q0);
  and and_7 (and_7_out, Q1, not_58_out, CLR_B);
  not not_59 (not_59_out, Q1);
  and and_8 (WR, not_59_out, Q0);
  and and_9 (and_9_out, not_1_out, not_2_out, not_3_out, not_4_out);
  and and_10 (and_10_out, not_5_out, not_6_out, not_7_out, not_8_out);
  and and_11 (and_11_out, not_9_out, not_10_out, not_11_out, not_12_out);
  and and_12 (and_12_out, not_13_out, not_14_out, not_15_out, not_16_out);
  and and_13 (and_13_out, not_17_out, not_18_out, not_19_out, not_20_out);
  and and_14 (and_14_out, not_21_out, not_22_out, RD_B, not_23_out, not_24_out);
  and and_15 (and_15_out, not_25_out, not_26_out, CLR_B, CLRMAX);
  and and_16 (and_16_out, not_27_out, not_28_out, not_29_out, not_30_out);
  and and_17 (and_17_out, not_31_out, not_32_out, not_33_out, not_34_out);
  and and_18 (and_18_out, not_35_out, not_36_out, not_37_out, not_38_out);
  and and_19 (and_19_out, not_39_out, not_40_out, not_41_out, not_42_out);
  and and_20 (and_20_out, not_43_out, not_44_out, not_45_out, not_46_out);
  and and_21 (and_21_out, not_47_out, not_48_out, not_49_out, WR_B, not_50_out);
  and and_22 (and_22_out, not_51_out, not_52_out, CLR_B, CLRMAX);
  or or_1 (D1, and_9_out, and_10_out, and_11_out, and_12_out, and_13_out, and_14_out, and_15_out);
  or or_2 (D0, and_16_out, and_17_out, and_18_out, and_19_out, and_20_out, and_21_out, and_22_out);
  or or_3 (RD, and_2_out, and_3_out, and_4_out, and_5_out, and_6_out, and_7_out);
endmodule

module BLOCO_OPERACIONAL (
  input  WR,
  input  RD,
  input  CLK,
  input  [3:0] valor,
  input  CLR,
  output [3:0] WRVA,
  output [3:0] RDVA,
  output [3:0] svalor,
  output EM,
  output FU
);

  wire and_3_out, and_4_out, comparator_1_eq, multiplexer_2_out, multiplexer_3_out, OPB, or_1_out;
  wire [3:0] multiplexer_1_out;

  Counter #(.width(4), .max('hf)) counter_1 (
    .Q(WRVA), .clk(WR), .clr(CLR));  // open: load, D, count, carry, preset, down
  Multiplexer #(.width(4), .enable("false")) multiplexer_1 (.in0(WRVA), .in1(RDVA), .out(multiplexer_1_out), .sel(RD));
  Comparator #(.width(4), .mode("unsigned")) comparator_1 (.a(WRVA), .b(RDVA), .eq(comparator_1_eq));  // open: gt, lt
  Counter #(.width(4), .max('hf)) counter_2 (
    .Q(RDVA), .clk(RD), .clr(CLR));  // open: load, D, count, carry, preset, down
  and and_1 (EM, ~OPB, comparator_1_eq);  // AND_Gate
  and and_2 (FU, comparator_1_eq, OPB);
  Multiplexer #(.enable("false")) multiplexer_2 (.in0(CLK), .in1(1'b0), .out(multiplexer_2_out), .sel(RD));
  RAM #(.addrWidth(4), .dataWidth(4), .bus("separate"), .Select("low")) ram_1 (
    .addr(multiplexer_1_out), .din(valor), .data(svalor), .str(WR), .clk(multiplexer_2_out), .ld(RD),
    .clr(CLR));  // open: sel
  and and_3 (and_3_out, RD, CLK);
  and and_4 (and_4_out, CLK, WR);
  Multiplexer #(.enable("false")) multiplexer_3 (.in0(1'b1), .in1(1'b0), .out(multiplexer_3_out), .sel(RD));
  or or_1 (or_1_out, and_3_out, and_4_out);
  D_Flip_Flop d_ff_1 (.clk(or_1_out), .D(multiplexer_3_out), .Q(OPB), .reset(CLR));  // open: Qn, preset

  // Other names for the same wires on the sheet: RDV[3:0] = RDVA; SRD = RD; SWR = WR; WRV[3:0] = WRVA

  // Notes on the sheet:
  //   EM = 1, nao pode ler
  //   FU = 1, nao pode escrever
endmodule

module BLOCO_DE_CONTROLE (
  input  CLRB,
  input  RDB,
  input  WRB,
  input  EM,
  input  FU,
  input  in_6,
  output CLR,
  output RD,
  output WR
);

  wire buttonactive_1_out_3, buttonactive_2_out_3, D0, D1, not_1_out, Q0, Q1;

  ButtonActive buttonactive_1 (.T(RDB), .CLK(in_6), .out_3(buttonactive_1_out_3));
  ButtonActive buttonactive_2 (.T(WRB), .CLK(in_6), .out_3(buttonactive_2_out_3));
  not not_1 (not_1_out, CLRB);
  MLL mll_1 (
    .Q1(Q1), .Q0(Q0), .CLR_B(not_1_out), .CLRMAX(1'b0), .RD_B(buttonactive_1_out_3),
    .WR_B(buttonactive_2_out_3), .EM(EM), .FU(FU), .D1(D1), .D0(D0), .CLR(CLR), .RD(RD), .WR(WR));
  D_Flip_Flop d_ff_1 (.clk(in_6), .D(D1), .Q(Q1));  // open: Qn, preset, reset
  D_Flip_Flop d_ff_2 (.clk(in_6), .D(D0), .Q(Q0));  // open: Qn, preset, reset

  // Other names for the same wires on the sheet: CLK = in_6
endmodule

module Button (
  input  Q1,
  input  Q0,
  input  T,
  output D1,
  output D0,
  output PRESS
);

  wire and_1_out, and_2_out, not_1_out, not_2_out, not_3_out, not_4_out, not_5_out;

  not not_1 (not_1_out, Q1);
  not not_2 (not_2_out, Q0);
  not not_3 (not_3_out, Q1);
  not not_4 (not_4_out, Q0);
  not not_5 (not_5_out, Q1);
  and and_1 (and_1_out, not_1_out, Q0);
  and and_2 (and_2_out, Q1, not_2_out, T);
  and and_3 (D0, not_3_out, not_4_out, T);
  and and_4 (PRESS, not_5_out, Q0);
  or or_1 (D1, and_1_out, and_2_out);
endmodule

module ButtonActive (
  input  T,
  input  CLK,
  output out_3
);

  wire button_1_d0, button_1_d1, d_ff_1_q, d_ff_2_q;

  Button button_1 (.Q1(d_ff_1_q), .Q0(d_ff_2_q), .T(T), .D1(button_1_d1), .D0(button_1_d0), .PRESS(out_3));
  D_Flip_Flop d_ff_1 (.clk(CLK), .D(button_1_d1), .Q(d_ff_1_q));  // open: Qn, preset, reset
  D_Flip_Flop d_ff_2 (.clk(CLK), .D(button_1_d0), .Q(d_ff_2_q));  // open: Qn, preset, reset

  // Notes on the sheet:
  //   BOTAO BS
endmodule
