// Logisim project TEO_FINAL.circ as structural Verilog: 8 circuits, main circuit main
module main (
  input  [12:0] in_1,
  input  CLRB,
  input  RDB,
  input  WRB,
  output [3:0] WR,
  output [3:0] RD,
  output [12:0] OUT
);

  wire bloco_de_controle_1_clr, bloco_de_controle_1_rd, bloco_de_controle_1_wr, bloco_operacional_1_em,
       bloco_operacional_1_fu, clock_1_out;

  Clock clock_1 (.out(clock_1_out));
  BLOCO_DE_CONTROLE bloco_de_controle_1 (
    .EM(bloco_operacional_1_em), .FU(bloco_operacional_1_fu), .CLR(bloco_de_controle_1_clr),
    .RD(bloco_de_controle_1_rd), .WR(bloco_de_controle_1_wr), .in_6(clock_1_out), .RDB(RDB), .WRB(WRB),
    .CLRB(CLRB));
  BLOCO_OPERACIONAL bloco_operacional_1 (
    .WR(bloco_de_controle_1_wr), .RD(bloco_de_controle_1_rd), .CLR(bloco_de_controle_1_clr),
    .CLK(clock_1_out), .WRVA(WR), .RDVA(RD), .EM(bloco_operacional_1_em), .FU(bloco_operacional_1_fu),
    .valor(in_1), .OUTvalor(OUT));
  LED EM (.in(bloco_operacional_1_em));
  LED FU (.in(bloco_operacional_1_fu));
endmodule

module MLL (
  input  Q1,
  input  Q0,
  input  CLR_B,
  input  RD_B,
  input  WR_B,
  input  EM,
  input  FU,
  output D1,
  output D0,
  output CLR,
  output RD,
  output WR
);

  wire and_2_out, and_3_out, and_4_out, and_5_out, and_6_out, and_7_out, and_9_out, and_10_out, and_11_out,
       and_12_out, and_13_out, and_14_out, and_15_out, and_16_out, and_17_out, and_18_out, and_19_out,
       and_20_out, and_21_out, and_22_out, not_1_out, not_2_out, not_3_out, not_4_out, not_5_out, not_6_out,
       not_7_out, not_8_out, not_9_out, not_10_out, not_11_out, not_12_out, not_13_out, not_14_out,
       not_15_out, not_16_out, not_17_out, not_18_out, not_19_out, not_20_out, not_21_out, not_22_out,
       not_23_out, not_24_out, not_25_out, not_26_out, not_27_out, not_28_out, not_29_out, not_30_out,
       not_31_out, not_32_out, not_33_out, not_34_out, not_35_out, not_36_out, not_37_out, not_38_out,
       not_39_out, not_40_out, not_41_out, not_42_out, not_43_out, not_44_out, not_45_out, not_46_out,
       not_47_out, not_48_out, not_49_out, not_50_out, not_51_out, not_52_out, not_53_out, not_54_out,
       not_55_out, not_56_out, not_57_out, not_58_out, not_59_out;

  not not_1 (not_1_out, Q1);
  not not_2 (not_2_out, Q0);
  not not_3 (not_3_out, CLR_B);
  not not_4 (not_4_out, 1'b0);
  not not_5 (not_5_out, Q1);
  not not_6 (not_6_out, Q0);
  not not_7 (not_7_out, CLR_B);
  not not_8 (not_8_out, RD_B);
  not not_9 (not_9_out, Q1);
  not not_10 (not_10_out, Q0);
  not not_11 (not_11_out, CLR_B);
  not not_12 (not_12_out, WR_B);
  not not_13 (not_13_out, Q1);
  not not_14 (not_14_out, Q0);
  not not_15 (not_15_out, CLR_B);
  not not_16 (not_16_out, EM);
  not not_17 (not_17_out, Q1);
  not not_18 (not_18_out, Q0);
  not not_19 (not_19_out, CLR_B);
  not not_20 (not_20_out, FU);
  not not_21 (not_21_out, Q1);
  not not_22 (not_22_out, Q0);
  not not_23 (not_23_out, WR_B);
  not not_24 (not_24_out, EM);
  not not_25 (not_25_out, Q1);
  not not_26 (not_26_out, Q0);
  not not_27 (not_27_out, Q1);
  not not_28 (not_28_out, Q0);
  not not_29 (not_29_out, CLR_B);
  not not_30 (not_30_out, 1'b0);
  not not_31 (not_31_out, Q1);
  not not_32 (not_32_out, Q0);
  not not_33 (not_33_out, CLR_B);
  not not_34 (not_34_out, RD_B);
  not not_35 (not_35_out, Q1);
  not not_36 (not_36_out, Q0);
  not not_37 (not_37_out, CLR_B);
  not not_38 (not_38_out, WR_B);
  not not_39 (not_39_out, Q1);
  not not_40 (not_40_out, Q0);
  not not_41 (not_41_out, CLR_B);
  not not_42 (not_42_out, EM);
  not not_43 (not_43_out, Q1);
  not not_44 (not_44_out, Q0);
  not not_45 (not_45_out, CLR_B);
  not not_46 (not_46_out, FU);
  not not_47 (not_47_out, Q1);
  not not_48 (not_48_out, Q0);
  not not_49 (not_49_out, RD_B);
  not not_50 (not_50_out, FU);
  not not_51 (not_51_out, Q1);
  not not_52 (not_52_out, Q0);
  and and_1 (CLR, Q1, Q0);
  not not_53 (not_53_out, Q0);
  and and_2 (and_2_out, Q1, not_53_out, FU);
  and and_3 (and_3_out, Q1, not_54_out, EM);
  not not_54 (not_54_out, Q0);
  and and_4 (and_4_out, Q1, not_55_out, WR_B);
  not not_55 (not_55_out, Q0);
  not not_56 (not_56_out, Q0);
  and and_5 (and_5_out, Q1, not_56_out, RD_B);
  not not_57 (not_57_out, Q0);
  and and_6 (and_6_out, Q1, not_57_out, 1'b0);
  and and_7 (and_7_out, Q1, not_58_out, CLR_B);
  not not_58 (not_58_out, Q0);
  not not_59 (not_59_out, Q1);
  and and_8 (WR, not_59_out, Q0);
  and and_9 (and_9_out, not_1_out, not_2_out, not_3_out, not_4_out);
  and and_10 (and_10_out, not_5_out, not_6_out, not_7_out, not_8_out);
  and and_11 (and_11_out, not_9_out, not_10_out, not_11_out, not_12_out);
  and and_12 (and_12_out, not_13_out, not_14_out, not_15_out, not_16_out);
  and and_13 (and_13_out, not_17_out, not_18_out, not_19_out, not_20_out);
  and and_14 (and_14_out, not_21_out, not_22_out, RD_B, not_23_out, not_24_out);
  and and_15 (and_15_out, not_25_out, not_26_out, CLR_B, 1'b0);
  and and_16 (and_16_out, not_27_out, not_28_out, not_29_out, not_30_out);
  and and_17 (and_17_out, not_31_out, not_32_out, not_33_out, not_34_out);
  and and_18 (and_18_out, not_35_out, not_36_out, not_37_out, not_38_out);
  and and_19 (and_19_out, not_39_out, not_40_out, not_41_out, not_42_out);
  and and_20 (and_20_out, not_43_out, not_44_out, not_45_out, not_46_out);
  and and_21 (and_21_out, not_47_out, not_48_out, not_49_out, WR_B, not_50_out);
  and and_22 (and_22_out, not_51_out, not_52_out, CLR_B, 1'b0);
  or or_1 (D1, and_9_out, and_10_out, and_11_out, and_12_out, and_13_out, and_14_out, and_15_out);
  or or_2 (D0, and_16_out, and_17_out, and_18_out, and_19_out, and_20_out, and_21_out, and_22_out);
  or or_3 (RD, and_2_out, and_3_out, and_4_out, and_5_out, and_6_out, and_7_out);
endmodule

module BLOCO_OPERACIONAL (
  input  WR,
  input  RD,
  input  CLK,
  input  CLR,
  input  [12:0] valor,
  output [3:0] WRVA,
  output [3:0] RDVA,
  output [12:0] OUTvalor,
  output EM,
  output FU
);

  wire comparator_1_eq, multiplexer_1_out, OPB, or_1_out;

  Counter #(.width(4), .max('hf)) counter_1 (
    .count(WR), .Q(WRVA), .clk(CLK), .clr(CLR));  // open: load, D, carry, preset, down
  Comparator #(.width(4), .mode("unsigned")) comparator_1 (.a(WRVA), .b(RDVA), .eq(comparator_1_eq));  // open: gt, lt
  Counter #(.width(4), .max('hf)) counter_2 (
    .count(RD), .Q(RDVA), .clk(CLK), .clr(CLR));  // open: load, D, carry, preset, down
  and and_1 (EM, ~OPB, comparator_1_eq);  // AND_Gate
  and and_2 (FU, comparator_1_eq, OPB);
  BANCO banco_1 (
    .WD0(valor[0]), .in_2(valor[1]), .in_3(valor[2]), .in_4(valor[3]), .in_5(valor[4]), .in_6(valor[5]),
    .in_7(valor[6]), .in_8(valor[7]), .in_9(valor[8]), .in_10(valor[9]), .in_11(valor[10]),
    .in_12(valor[11]), .WD12(valor[12]), .RD0(OUTvalor[0]), .out_26(OUTvalor[1]), .out_27(OUTvalor[2]),
    .out_28(OUTvalor[3]), .out_29(OUTvalor[4]), .out_30(OUTvalor[5]), .out_31(OUTvalor[6]),
    .out_32(OUTvalor[7]), .out_33(OUTvalor[8]), .out_34(OUTvalor[9]), .out_35(OUTvalor[10]),
    .out_36(OUTvalor[11]), .RD12(OUTvalor[12]), .W0(WRVA[0]), .in_18(WRVA[1]), .in_19(WRVA[2]), .W3(WRVA[3]),
    .R0(RDVA[0]), .in_22(RDVA[1]), .in_23(RDVA[2]), .R3(RDVA[3]), .WR(WR), .CLR(CLR), .in_15(CLK));
  Multiplexer #(.enable("false")) multiplexer_1 (.in0(1'b1), .in1(1'b0), .out(multiplexer_1_out), .sel(RD));
  or or_1 (or_1_out, RD, WR);
  D_Flip_Flop #(.enable("true")) d_ff_1 (
    .clk(CLK), .D(multiplexer_1_out), .Q(OPB), .en(or_1_out), .reset(CLR));  // open: Qn, preset

  // Other names for the same wires on the sheet: RDV[3:0] = RDVA; SRD = RD; SWR = WR; WRV[3:0] = WRVA

  // Notes on the sheet:
  //   EM = 1, nao pode ler
  //   FU = 1, nao pode escrever
endmodule

module BLOCO_DE_CONTROLE (
  input  CLRB,
  input  RDB,
  input  WRB,
  input  EM,
  input  FU,
  input  in_6,
  output CLR,
  output RD,
  output WR
);

  wire buttonactive_1_out_3, buttonactive_2_out_3, D0, D1, not_1_out, Q0, Q1;

  ButtonActive buttonactive_1 (.T(RDB), .CLK(in_6), .out_3(buttonactive_1_out_3));
  ButtonActive buttonactive_2 (.T(WRB), .CLK(in_6), .out_3(buttonactive_2_out_3));
  not not_1 (not_1_out, CLRB);
  MLL mll_1 (
    .Q1(Q1), .Q0(Q0), .CLR_B(not_1_out), .RD_B(buttonactive_1_out_3), .WR_B(buttonactive_2_out_3), .EM(EM),
    .FU(FU), .D1(D1), .D0(D0), .CLR(CLR), .RD(RD), .WR(WR));
  D_Flip_Flop d_ff_1 (.clk(in_6), .D(D1), .Q(Q1));  // open: Qn, preset, reset
  D_Flip_Flop d_ff_2 (.clk(in_6), .D(D0), .Q(Q0));  // open: Qn, preset, reset

  // Other names for the same wires on the sheet: CLK = in_6
endmodule

module Button (
  input  Q1,
  input  Q0,
  input  T,
  output D1,
  output D0,
  output PRESS
);

  wire and_1_out, and_2_out, not_1_out, not_2_out, not_3_out, not_4_out, not_5_out;

  not not_1 (not_1_out, Q1);
  not not_2 (not_2_out, Q0);
  not not_3 (not_3_out, Q1);
  not not_4 (not_4_out, Q0);
  not not_5 (not_5_out, Q1);
  and and_1 (and_1_out, not_1_out, Q0);
  and and_2 (and_2_out, Q1, not_2_out, T);
  and and_3 (D0, not_3_out, not_4_out, T);
  and and_4 (PRESS, not_5_out, Q0);
  or or_1 (D1, and_1_out, and_2_out);
endmodule

module ButtonActive (
  input  T,
  input  CLK,
  output out_3
);

  wire button_1_d0, button_1_d1, d_ff_1_q, d_ff_2_q;

  Button button_1 (.Q1(d_ff_1_q), .Q0(d_ff_2_q), .T(T), .D1(button_1_d1), .D0(button_1_d0), .PRESS(out_3));
  D_Flip_Flop d_ff_1 (.clk(CLK), .D(button_1_d1), .Q(d_ff_1_q));  // open: Qn, preset, reset
  D_Flip_Flop d_ff_2 (.clk(CLK), .D(button_1_d0), .Q(d_ff_2_q));  // open: Qn, preset, reset

  // Notes on the sheet:
  //   BOTAO BS
endmodule

module BANCO (
  input  WD0,
  input  in_2,
  input  in_3,
  input  in_4,
  input  in_5,
  input  in_6,
  input  in_7,
  input  in_8,
  input  in_9,
  input  in_10,
  input  in_11,
  input  in_12,
  input  WD12,
  input  WR,
  input  in_15,
  input  CLR,
  input  W0,
  input  in_18,
  input  in_19,
  input  W3,
  input  R0,
  input  in_22,
  input  in_23,
  input  R3,
  output RD0,
  output out_26,
  output out_27,
  output out_28,
  output out_29,
  output out_30,
  output out_31,
  output out_32,
  output out_33,
  output out_34,
  output out_35,
  output out_36,
  output RD12
);

  wire LD0, LD1, LD2, LD3, LD4, LD5, LD6, LD7, LD8, LD9, LD10, LD11, LD12, LD13, LD14, LD15, REG1D0, REG1D1,
       REG1D2, REG1D3, REG1D4, REG1D5, REG1D6, REG1D7, REG1D8, REG1D9, REG1D10, REG1D11, REG1D12, REG2D0,
       REG2D1, REG2D2, REG2D3, REG2D4, REG2D5, REG2D6, REG2D7, REG2D8, REG2D9, REG2D10, REG2D11, REG2D12,
       REG3D0, REG3D1, REG3D2, REG3D3, REG3D4, REG3D5, REG3D6, REG3D7, REG3D8, REG3D9, REG3D10, REG3D11,
       REG3D12, REG4D0, REG4D1, REG4D2, REG4D3, REG4D4, REG4D5, REG4D6, REG4D7, REG4D8, REG4D9, REG4D10,
       REG4D11, REG4D12, REG5D0, REG5D1, REG5D2, REG5D3, REG5D4, REG5D5, REG5D6, REG5D7, REG5D8, REG5D9,
       REG5D10, REG5D11, REG5D12, REG6D0, REG6D1, REG6D2, REG6D3, REG6D4, REG6D5, REG6D6, REG6D7, REG6D8,
       REG6D9, REG6D10, REG6D11, REG6D12, REG7D0, REG7D1, REG7D2, REG7D3, REG7D4, REG7D5, REG7D6, REG7D7,
       REG7D8, REG7D9, REG7D10, REG7D11, REG7D12, REG8D0, REG8D1, REG8D2, REG8D3, REG8D4, REG8D5, REG8D6,
       REG8D7, REG8D8, REG8D9, REG8D10, REG8D11, REG8D12, REG9D0, REG9D1, REG9D2, REG9D3, REG9D4, REG9D5,
       REG9D6, REG9D7, REG9D8, REG9D9, REG9D10, REG9D11, REG9D12, REG10D0, REG10D1, REG10D2, REG10D3,
       REG10D4, REG10D5, REG10D6, REG10D7, REG10D8, REG10D9, REG10D10, REG10D11, REG10D12, REG11D0, REG11D1,
       REG11D2, REG11D3, REG11D4, REG11D5, REG11D6, REG11D7, REG11D8, REG11D9, REG11D10, REG11D11, REG11D12,
       REG12D0, REG12D1, REG12D2, REG12D3, REG12D4, REG12D5, REG12D6, REG12D7, REG12D8, REG12D9, REG12D10,
       REG12D11, REG12D12, REG13D0, REG13D1, REG13D2, REG13D3, REG13D4, REG13D5, REG13D6, REG13D7, REG13D8,
       REG13D9, REG13D10, REG13D11, REG13D12, REG14D0, REG14D1, REG14D2, REG14D3, REG14D4, REG14D5, REG14D6,
       REG14D7, REG14D8, REG14D9, REG14D10, REG14D11, REG14D12, REG15D0, REG15D1, REG15D2, REG15D3, REG15D4,
       REG15D5, REG15D6, REG15D7, REG15D8, REG15D9, REG15D10, REG15D11, REG15D12, REGD0, REGD1, REGD2, REGD3,
       REGD4, REGD5, REGD6, REGD7, REGD8, REGD9, REGD10, REGD11, REGD12;

  Demultiplexer #(.select(4), .disabled(0)) demultiplexer_1 (
    .out0(LD0), .out1(LD1), .out2(LD2), .out3(LD3), .out4(LD4), .out5(LD5), .out6(LD6), .out7(LD7),
    .out8(LD8), .out9(LD9), .out10(LD10), .out11(LD11), .out12(LD12), .out13(LD13), .out14(LD14),
    .out15(LD15), .in(1'b1), .sel({W3, in_19, in_18, W0}), .en(WR));
  REG13 reg13_1 (
    .Q0(WD0), .Q1(in_2), .Q2(in_3), .Q3(in_4), .Q4(in_5), .Q5(in_6), .Q6(in_7), .Q7(in_8), .Q8(in_9),
    .Q9(in_10), .Q10(in_11), .Q11(in_12), .Q12(WD12), .D0(REG2D0), .D1(REG2D1), .D2(REG2D2), .D3(REG2D3),
    .D4(REG2D4), .D5(REG2D5), .D6(REG2D6), .D7(REG2D7), .D8(REG2D8), .D9(REG2D9), .D10(REG2D10),
    .D11(REG2D11), .D12(REG2D12), .LD(LD2), .CLR(CLR), .CLK(in_15));
  REG13 reg13_2 (
    .Q0(WD0), .Q1(in_2), .Q2(in_3), .Q3(in_4), .Q4(in_5), .Q5(in_6), .Q6(in_7), .Q7(in_8), .Q8(in_9),
    .Q9(in_10), .Q10(in_11), .Q11(in_12), .Q12(WD12), .D0(REG3D0), .D1(REG3D1), .D2(REG3D2), .D3(REG3D3),
    .D4(REG3D4), .D5(REG3D5), .D6(REG3D6), .D7(REG3D7), .D8(REG3D8), .D9(REG3D9), .D10(REG3D10),
    .D11(REG3D11), .D12(REG3D12), .LD(LD3), .CLR(CLR), .CLK(in_15));
  REG13 reg13_3 (
    .Q0(WD0), .Q1(in_2), .Q2(in_3), .Q3(in_4), .Q4(in_5), .Q5(in_6), .Q6(in_7), .Q7(in_8), .Q8(in_9),
    .Q9(in_10), .Q10(in_11), .Q11(in_12), .Q12(WD12), .D0(REG4D0), .D1(REG4D1), .D2(REG4D2), .D3(REG4D3),
    .D4(REG4D4), .D5(REG4D5), .D6(REG4D6), .D7(REG4D7), .D8(REG4D8), .D9(REG4D9), .D10(REG4D10),
    .D11(REG4D11), .D12(REG4D12), .LD(LD4), .CLR(CLR), .CLK(in_15));
  REG13 reg13_4 (
    .Q0(WD0), .Q1(in_2), .Q2(in_3), .Q3(in_4), .Q4(in_5), .Q5(in_6), .Q6(in_7), .Q7(in_8), .Q8(in_9),
    .Q9(in_10), .Q10(in_11), .Q11(in_12), .Q12(WD12), .D0(REG5D0), .D1(REG5D1), .D2(REG5D2), .D3(REG5D3),
    .D4(REG5D4), .D5(REG5D5), .D6(REG5D6), .D7(REG5D7), .D8(REG5D8), .D9(REG5D9), .D10(REG5D10),
    .D11(REG5D11), .D12(REG5D12), .LD(LD5), .CLR(CLR), .CLK(in_15));
  REG13 reg13_5 (
    .Q0(WD0), .Q1(in_2), .Q2(in_3), .Q3(in_4), .Q4(in_5), .Q5(in_6), .Q6(in_7), .Q7(in_8), .Q8(in_9),
    .Q9(in_10), .Q10(in_11), .Q11(in_12), .Q12(WD12), .D0(REG6D0), .D1(REG6D1), .D2(REG6D2), .D3(REG6D3),
    .D4(REG6D4), .D5(REG6D5), .D6(REG6D6), .D7(REG6D7), .D8(REG6D8), .D9(REG6D9), .D10(REG6D10),
    .D11(REG6D11), .D12(REG6D12), .LD(LD6), .CLR(CLR), .CLK(in_15));
  REG13 reg13_6 (
    .Q0(WD0), .Q1(in_2), .Q2(in_3), .Q3(in_4), .Q4(in_5), .Q5(in_6), .Q6(in_7), .Q7(in_8), .Q8(in_9),
    .Q9(in_10), .Q10(in_11), .Q11(in_12), .Q12(WD12), .D0(REGD0), .D1(REGD1), .D2(REGD2), .D3(REGD3),
    .D4(REGD4), .D5(REGD5), .D6(REGD6), .D7(REGD7), .D8(REGD8), .D9(REGD9), .D10(REGD10), .D11(REGD11),
    .D12(REGD12), .LD(LD0), .CLR(CLR), .CLK(in_15));
  REG13 reg13_7 (
    .Q0(WD0), .Q1(in_2), .Q2(in_3), .Q3(in_4), .Q4(in_5), .Q5(in_6), .Q6(in_7), .Q7(in_8), .Q8(in_9),
    .Q9(in_10), .Q10(in_11), .Q11(in_12), .Q12(WD12), .D0(REG1D0), .D1(REG1D1), .D2(REG1D2), .D3(REG1D3),
    .D4(REG1D4), .D5(REG1D5), .D6(REG1D6), .D7(REG1D7), .D8(REG1D8), .D9(REG1D9), .D10(REG1D10),
    .D11(REG1D11), .D12(REG1D12), .LD(LD1), .CLR(CLR), .CLK(in_15));
  Multiplexer #(.select(4), .width(13), .enable("false")) multiplexer_1 (
    .in0({REGD12, REGD11, REGD10, REGD9, REGD8, REGD7, REGD6, REGD5, REGD4, REGD3, REGD2, REGD1, REGD0}),
    .in1({REG1D12, REG1D11, REG1D10, REG1D9, REG1D8, REG1D7, REG1D6, REG1D5, REG1D4, REG1D3, REG1D2, REG1D1, REG1D0}),
    .in2({REG2D12, REG2D11, REG2D10, REG2D9, REG2D8, REG2D7, REG2D6, REG2D5, REG2D4, REG2D3, REG2D2, REG2D1, REG2D0}),
    .in3({REG3D12, REG3D11, REG3D10, REG3D9, REG3D8, REG3D7, REG3D6, REG3D5, REG3D4, REG3D3, REG3D2, REG3D1, REG3D0}),
    .in4({REG4D12, REG4D11, REG4D10, REG4D9, REG4D8, REG4D7, REG4D6, REG4D5, REG4D4, REG4D3, REG4D2, REG4D1, REG4D0}),
    .in5({REG5D12, REG5D11, REG5D10, REG5D9, REG5D8, REG5D7, REG5D6, REG5D5, REG5D4, REG5D3, REG5D2, REG5D1, REG5D0}),
    .in6({REG6D12, REG6D11, REG6D10, REG6D9, REG6D8, REG6D7, REG6D6, REG6D5, REG6D4, REG6D3, REG6D2, REG6D1, REG6D0}),
    .in7({REG7D12, REG7D11, REG7D10, REG7D9, REG7D8, REG7D7, REG7D6, REG7D5, REG7D4, REG7D3, REG7D2, REG7D1, REG7D0}),
    .in8({REG8D12, REG8D11, REG8D10, REG8D9, REG8D8, REG8D7, REG8D6, REG8D5, REG8D4, REG8D3, REG8D2, REG8D1, REG8D0}),
    .in9({REG9D12, REG9D11, REG9D10, REG9D9, REG9D8, REG9D7, REG9D6, REG9D5, REG9D4, REG9D3, REG9D2, REG9D1, REG9D0}),
    .in10({REG10D12, REG10D11, REG10D10, REG10D9, REG10D8, REG10D7, REG10D6, REG10D5, REG10D4, REG10D3, REG10D2, REG10D1, REG10D0}),
    .in11({REG11D12, REG11D11, REG11D10, REG11D9, REG11D8, REG11D7, REG11D6, REG11D5, REG11D4, REG11D3, REG11D2, REG11D1, REG11D0}),
    .in12({REG12D12, REG12D11, REG12D10, REG12D9, REG12D8, REG12D7, REG12D6, REG12D5, REG12D4, REG12D3, REG12D2, REG12D1, REG12D0}),
    .in13({REG13D12, REG13D11, REG13D10, REG13D9, REG13D8, REG13D7, REG13D6, REG13D5, REG13D4, REG13D3, REG13D2, REG13D1, REG13D0}),
    .in14({REG14D12, REG14D11, REG14D10, REG14D9, REG14D8, REG14D7, REG14D6, REG14D5, REG14D4, REG14D3, REG14D2, REG14D1, REG14D0}),
    .in15({REG15D12, REG15D11, REG15D10, REG15D9, REG15D8, REG15D7, REG15D6, REG15D5, REG15D4, REG15D3, REG15D2, REG15D1, REG15D0}),
    .out({RD12, out_36, out_35, out_34, out_33, out_32, out_31, out_30, out_29, out_28, out_27, out_26, RD0}),
    .sel({R3, in_23, in_22, R0}));
  REG13 reg13_8 (
    .Q0(WD0), .Q1(in_2), .Q2(in_3), .Q3(in_4), .Q4(in_5), .Q5(in_6), .Q6(in_7), .Q7(in_8), .Q8(in_9),
    .Q9(in_10), .Q10(in_11), .Q11(in_12), .Q12(WD12), .D0(REG8D0), .D1(REG8D1), .D2(REG8D2), .D3(REG8D3),
    .D4(REG8D4), .D5(REG8D5), .D6(REG8D6), .D7(REG8D7), .D8(REG8D8), .D9(REG8D9), .D10(REG8D10),
    .D11(REG8D11), .D12(REG8D12), .LD(LD8), .CLR(CLR), .CLK(in_15));
  REG13 reg13_9 (
    .Q0(WD0), .Q1(in_2), .Q2(in_3), .Q3(in_4), .Q4(in_5), .Q5(in_6), .Q6(in_7), .Q7(in_8), .Q8(in_9),
    .Q9(in_10), .Q10(in_11), .Q11(in_12), .Q12(WD12), .D0(REG9D0), .D1(REG9D1), .D2(REG9D2), .D3(REG9D3),
    .D4(REG9D4), .D5(REG9D5), .D6(REG9D6), .D7(REG9D7), .D8(REG9D8), .D9(REG9D9), .D10(REG9D10),
    .D11(REG9D11), .D12(REG9D12), .LD(LD9), .CLR(CLR), .CLK(in_15));
  REG13 reg13_10 (
    .Q0(WD0), .Q1(in_2), .Q2(in_3), .Q3(in_4), .Q4(in_5), .Q5(in_6), .Q6(in_7), .Q7(in_8), .Q8(in_9),
    .Q9(in_10), .Q10(in_11), .Q11(in_12), .Q12(WD12), .D0(REG10D0), .D1(REG10D1), .D2(REG10D2), .D3(REG10D3),
    .D4(REG10D4), .D5(REG10D5), .D6(REG10D6), .D7(REG10D7), .D8(REG10D8), .D9(REG10D9), .D10(REG10D10),
    .D11(REG10D11), .D12(REG10D12), .LD(LD10), .CLR(CLR), .CLK(in_15));
  REG13 reg13_11 (
    .Q0(WD0), .Q1(in_2), .Q2(in_3), .Q3(in_4), .Q4(in_5), .Q5(in_6), .Q6(in_7), .Q7(in_8), .Q8(in_9),
    .Q9(in_10), .Q10(in_11), .Q11(in_12), .Q12(WD12), .D0(REG11D0), .D1(REG11D1), .D2(REG11D2), .D3(REG11D3),
    .D4(REG11D4), .D5(REG11D5), .D6(REG11D6), .D7(REG11D7), .D8(REG11D8), .D9(REG11D9), .D10(REG11D10),
    .D11(REG11D11), .D12(REG11D12), .LD(LD11), .CLR(CLR), .CLK(in_15));
  REG13 reg13_12 (
    .Q0(WD0), .Q1(in_2), .Q2(in_3), .Q3(in_4), .Q4(in_5), .Q5(in_6), .Q6(in_7), .Q7(in_8), .Q8(in_9),
    .Q9(in_10), .Q10(in_11), .Q11(in_12), .Q12(WD12), .D0(REG12D0), .D1(REG12D1), .D2(REG12D2), .D3(REG12D3),
    .D4(REG12D4), .D5(REG12D5), .D6(REG12D6), .D7(REG12D7), .D8(REG12D8), .D9(REG12D9), .D10(REG12D10),
    .D11(REG12D11), .D12(REG12D12), .LD(LD12), .CLR(CLR), .CLK(in_15));
  REG13 reg13_13 (
    .Q0(WD0), .Q1(in_2), .Q2(in_3), .Q3(in_4), .Q4(in_5), .Q5(in_6), .Q6(in_7), .Q7(in_8), .Q8(in_9),
    .Q9(in_10), .Q10(in_11), .Q11(in_12), .Q12(WD12), .D0(REG13D0), .D1(REG13D1), .D2(REG13D2), .D3(REG13D3),
    .D4(REG13D4), .D5(REG13D5), .D6(REG13D6), .D7(REG13D7), .D8(REG13D8), .D9(REG13D9), .D10(REG13D10),
    .D11(REG13D11), .D12(REG13D12), .LD(LD13), .CLR(CLR), .CLK(in_15));
  REG13 reg13_14 (
    .Q0(WD0), .Q1(in_2), .Q2(in_3), .Q3(in_4), .Q4(in_5), .Q5(in_6), .Q6(in_7), .Q7(in_8), .Q8(in_9),
    .Q9(in_10), .Q10(in_11), .Q11(in_12), .Q12(WD12), .D0(REG7D0), .D1(REG7D1), .D2(REG7D2), .D3(REG7D3),
    .D4(REG7D4), .D5(REG7D5), .D6(REG7D6), .D7(REG7D7), .D8(REG7D8), .D9(REG7D9), .D10(REG7D10),
    .D11(REG7D11), .D12(REG7D12), .LD(LD7), .CLR(CLR), .CLK(in_15));
  REG13 reg13_15 (
    .Q0(WD0), .Q1(in_2), .Q2(in_3), .Q3(in_4), .Q4(in_5), .Q5(in_6), .Q6(in_7), .Q7(in_8), .Q8(in_9),
    .Q9(in_10), .Q10(in_11), .Q11(in_12), .Q12(WD12), .D0(REG14D0), .D1(REG14D1), .D2(REG14D2), .D3(REG14D3),
    .D4(REG14D4), .D5(REG14D5), .D6(REG14D6), .D7(REG14D7), .D8(REG14D8), .D9(REG14D9), .D10(REG14D10),
    .D11(REG14D11), .D12(REG14D12), .LD(LD14), .CLR(CLR), .CLK(in_15));
  REG13 reg13_16 (
    .Q0(WD0), .Q1(in_2), .Q2(in_3), .Q3(in_4), .Q4(in_5), .Q5(in_6), .Q6(in_7), .Q7(in_8), .Q8(in_9),
    .Q9(in_10), .Q10(in_11), .Q11(in_12), .Q12(WD12), .D0(REG15D0), .D1(REG15D1), .D2(REG15D2), .D3(REG15D3),
    .D4(REG15D4), .D5(REG15D5), .D6(REG15D6), .D7(REG15D7), .D8(REG15D8), .D9(REG15D9), .D10(REG15D10),
    .D11(REG15D11), .D12(REG15D12), .LD(LD15), .CLR(CLR), .CLK(in_15));

  // Other names for the same wires on the sheet: W1 = in_18; W2 = in_19; R1 = in_22; R2 = in_23; RD1 = out_26;
  //   RD2 = out_27; RD3 = out_28; RD4 = out_29; RD5 = out_30; RD6 = out_31; RD7 = out_32; RD8 = out_33; RD9 = out_34;
  //   RD10 = out_35; RD11 = out_36; CLK = in_15; WD1 = in_2; WD2 = in_3; WD3 = in_4; WD4 = in_5; WD5 = in_6;
  //   WD6 = in_7; WD7 = in_8; WD8 = in_9; WD9 = in_10; WD10 = in_11; WD11 = in_12
endmodule

module REG13 (
  input  LD,
  input  CLK,
  input  Q0,
  input  Q1,
  input  Q2,
  input  Q3,
  input  Q4,
  input  Q5,
  input  Q6,
  input  CLR,
  input  Q7,
  input  Q8,
  input  Q9,
  input  Q10,
  input  Q11,
  input  Q12,
  output D0,
  output D1,
  output D2,
  output D3,
  output D4,
  output D5,
  output D6,
  output D7,
  output D8,
  output D9,
  output D10,
  output D11,
  output D12
);

  D_Flip_Flop #(.enable("true")) d_ff_1 (.clk(CLK), .D(Q0), .Q(D0), .en(LD), .reset(CLR));  // open: Qn, preset
  D_Flip_Flop #(.enable("true")) d_ff_2 (.clk(CLK), .D(Q7), .Q(D7), .en(LD), .reset(CLR));  // open: Qn, preset
  D_Flip_Flop #(.enable("true")) d_ff_3 (.clk(CLK), .D(Q1), .Q(D1), .en(LD), .reset(CLR));  // open: Qn, preset
  D_Flip_Flop #(.enable("true")) d_ff_4 (.clk(CLK), .D(Q8), .Q(D8), .en(LD), .reset(CLR));  // open: Qn, preset
  D_Flip_Flop #(.enable("true")) d_ff_5 (.clk(CLK), .D(Q2), .Q(D2), .en(LD), .reset(CLR));  // open: Qn, preset
  D_Flip_Flop #(.enable("true")) d_ff_6 (.clk(CLK), .D(Q9), .Q(D9), .en(LD), .reset(CLR));  // open: Qn, preset
  D_Flip_Flop #(.enable("true")) d_ff_7 (.clk(CLK), .D(Q3), .Q(D3), .en(LD), .reset(CLR));  // open: Qn, preset
  D_Flip_Flop #(.enable("true")) d_ff_8 (.clk(CLK), .D(Q10), .Q(D10), .en(LD), .reset(CLR));  // open: Qn, preset
  D_Flip_Flop #(.enable("true")) d_ff_9 (.clk(CLK), .D(Q4), .Q(D4), .en(LD), .reset(CLR));  // open: Qn, preset
  D_Flip_Flop #(.enable("true")) d_ff_10 (.clk(CLK), .D(Q11), .Q(D11), .en(LD), .reset(CLR));  // open: Qn, preset
  D_Flip_Flop #(.enable("true")) d_ff_11 (.clk(CLK), .D(Q5), .Q(D5), .en(LD), .reset(CLR));  // open: Qn, preset
  D_Flip_Flop #(.enable("true")) d_ff_12 (.clk(CLK), .D(Q12), .Q(D12), .en(LD), .reset(CLR));  // open: Qn, preset
  D_Flip_Flop #(.enable("true")) d_ff_13 (.clk(CLK), .D(Q6), .Q(D6), .en(LD), .reset(CLR));  // open: Qn, preset
endmodule
