// Logisim project banco_de_dados (1).circ as structural Verilog: 2 circuits, main circuit main
module main (
  input  in_1,
  input  in_2,
  input  in_3,
  input  in_4,
  input  in_5,
  input  in_6,
  input  in_7,
  input  in_8,
  input  in_9,
  input  in_10,
  input  in_11,
  input  in_12,
  input  in_13,
  input  in_14,
  input  in_15,
  input  in_16,
  input  in_17,
  input  in_18,
  input  in_19,
  input  in_20,
  input  in_21,
  input  in_22,
  input  in_23
);

  wire CLK, D0, D1, D2, D3, D4, D5, D6, D7, D8, D9, D10, D11, D12, D13, D14, D15, LD0, LD1, LD2, LD3, LD4,
       LD5, LD6, LD7, LD8, LD9, LD10, LD11, LD12, LD13, LD14, LD15, RD0, RD1, RD2, RD3, RD4, RD5, RD6, RD7,
       RD8, RD9, RD10, RD11, RD12, REG1D0, REG1D1, REG1D2, REG1D3, REG1D4, REG1D5, REG1D6, REG1D7, REG1D8,
       REG1D9, REG1D10, REG1D11, REG1D12, REG2D0, REG2D1, REG2D2, REG2D3, REG2D4, REG2D5, REG2D6, REG2D7,
       REG2D8, REG2D9, REG2D10, REG2D11, REG2D12, REG3D0, REG3D1, REG3D2, REG3D3, REG3D4, REG3D5, REG3D6,
       REG3D7, REG3D8, REG3D9, REG3D10, REG3D11, REG3D12, REG4D0, REG4D1, REG4D2, REG4D3, REG4D4, REG4D5,
       REG4D6, REG4D7, REG4D8, REG4D9, REG4D10, REG4D11, REG4D12, REG5D0, REG5D1, REG5D2, REG5D3, REG5D4,
       REG5D5, REG5D6, REG5D7, REG5D8, REG5D9, REG5D10, REG5D11, REG5D12, REG6D0, REG6D1, REG6D2, REG6D3,
       REG6D4, REG6D5, REG6D6, REG6D7, REG6D8, REG6D9, REG6D10, REG6D11, REG6D12, REG7D0, REG7D1, REG7D2,
       REG7D3, REG7D4, REG7D5, REG7D6, REG7D7, REG7D8, REG7D9, REG7D10, REG7D11, REG7D12, REG8D0, REG8D1,
       REG8D2, REG8D3, REG8D4, REG8D5, REG8D6, REG8D7, REG8D8, REG8D9, REG8D10, REG8D11, REG8D12, REG9D0,
       REG9D1, REG9D2, REG9D3, REG9D4, REG9D5, REG9D6, REG9D7, REG9D8, REG9D9, REG9D10, REG9D11, REG9D12,
       REG10D0, REG10D1, REG10D2, REG10D3, REG10D4, REG10D5, REG10D6, REG10D7, REG10D8, REG10D9, REG10D10,
       REG10D11, REG10D12, REG11D0, REG11D1, REG11D2, REG11D3, REG11D4, REG11D5, REG11D6, REG11D7, REG11D8,
       REG11D9, REG11D10, REG11D11, REG11D12, REG12D0, REG12D1, REG12D2, REG12D3, REG12D4, REG12D5, REG12D6,
       REG12D7, REG12D8, REG12D9, REG12D10, REG12D11, REG12D12, REG13D0, REG13D1, REG13D2, REG13D3, REG13D4,
       REG13D5, REG13D6, REG13D7, REG13D8, REG13D9, REG13D10, REG13D11, REG13D12, REG14D0, REG14D1, REG14D2,
       REG14D3, REG14D4, REG14D5, REG14D6, REG14D7, REG14D8, REG14D9, REG14D10, REG14D11, REG14D12, REG15D0,
       REG15D1, REG15D2, REG15D3, REG15D4, REG15D5, REG15D6, REG15D7, REG15D8, REG15D9, REG15D10, REG15D11,
       REG15D12, REGD0, REGD1, REGD2, REGD3, REGD4, REGD5, REGD6, REGD7, REGD8, REGD9, REGD10, REGD11, REGD12;

  Clock clock_1 (.out(CLK));
  Demultiplexer #(.select(4), .enable("false")) demultiplexer_1 (
    .out0(LD0), .out1(LD1), .out2(LD2), .out3(LD3), .out4(LD4), .out5(LD5), .out6(LD6), .out7(LD7),
    .out8(LD8), .out9(LD9), .out10(LD10), .out11(LD11), .out12(LD12), .out13(LD13), .out14(LD14),
    .out15(LD15), .in(1'b1), .sel({in_18, in_17, in_16, in_15}));
  REG13 reg13_1 (
    .CLOCK(CLK), .Q0(in_1), .Q1(in_2), .Q2(in_3), .Q3(in_4), .Q4(in_5), .Q5(in_6), .Q6(in_7), .Q7(in_8),
    .Q8(in_9), .Q9(in_10), .Q10(in_11), .Q11(in_12), .Q12(in_13), .D0(REG3D0), .D1(REG3D1), .D2(REG3D2),
    .D3(REG3D3), .D4(REG3D4), .D5(REG3D5), .D6(REG3D6), .D7(REG3D7), .D8(REG3D8), .D9(REG3D9), .D10(REG3D10),
    .D11(REG3D11), .D12(REG3D12), .CLR(in_19), .LD(LD3));
  REG13 reg13_2 (
    .CLOCK(CLK), .Q0(in_1), .Q1(in_2), .Q2(in_3), .Q3(in_4), .Q4(in_5), .Q5(in_6), .Q6(in_7), .Q7(in_8),
    .Q8(in_9), .Q9(in_10), .Q10(in_11), .Q11(in_12), .Q12(in_13), .D0(REG4D0), .D1(REG4D1), .D2(REG4D2),
    .D3(REG4D3), .D4(REG4D4), .D5(REG4D5), .D6(REG4D6), .D7(REG4D7), .D8(REG4D8), .D9(REG4D9), .D10(REG4D10),
    .D11(REG4D11), .D12(REG4D12), .CLR(in_19), .LD(LD4));
  REG13 reg13_3 (
    .CLOCK(CLK), .Q0(in_1), .Q1(in_2), .Q2(in_3), .Q3(in_4), .Q4(in_5), .Q5(in_6), .Q6(in_7), .Q7(in_8),
    .Q8(in_9), .Q9(in_10), .Q10(in_11), .Q11(in_12), .Q12(in_13), .D0(REG5D0), .D1(REG5D1), .D2(REG5D2),
    .D3(REG5D3), .D4(REG5D4), .D5(REG5D5), .D6(REG5D6), .D7(REG5D7), .D8(REG5D8), .D9(REG5D9), .D10(REG5D10),
    .D11(REG5D11), .D12(REG5D12), .CLR(in_19), .LD(LD5));
  REG13 reg13_4 (
    .CLOCK(CLK), .Q0(in_1), .Q1(in_2), .Q2(in_3), .Q3(in_4), .Q4(in_5), .Q5(in_6), .Q6(in_7), .Q7(in_8),
    .Q8(in_9), .Q9(in_10), .Q10(in_11), .Q11(in_12), .Q12(in_13), .D0(REG6D0), .D1(REG6D1), .D2(REG6D2),
    .D3(REG6D3), .D4(REG6D4), .D5(REG6D5), .D6(REG6D6), .D7(REG6D7), .D8(REG6D8), .D9(REG6D9), .D10(REG6D10),
    .D11(REG6D11), .D12(REG6D12), .CLR(in_19), .LD(LD6));
  REG13 reg13_5 (
    .CLOCK(CLK), .Q0(in_1), .Q1(in_2), .Q2(in_3), .Q3(in_4), .Q4(in_5), .Q5(in_6), .Q6(in_7), .Q7(in_8),
    .Q8(in_9), .Q9(in_10), .Q10(in_11), .Q11(in_12), .Q12(in_13), .D0(REGD0), .D1(REGD1), .D2(REGD2),
    .D3(REGD3), .D4(REGD4), .D5(REGD5), .D6(REGD6), .D7(REGD7), .D8(REGD8), .D9(REGD9), .D10(REGD10),
    .D11(REGD11), .D12(REGD12), .CLR(in_19), .LD(LD0));
  REG13 reg13_6 (
    .CLOCK(CLK), .Q0(in_1), .Q1(in_2), .Q2(in_3), .Q3(in_4), .Q4(in_5), .Q5(in_6), .Q6(in_7), .Q7(in_8),
    .Q8(in_9), .Q9(in_10), .Q10(in_11), .Q11(in_12), .Q12(in_13), .D0(REG1D0), .D1(REG1D1), .D2(REG1D2),
    .D3(REG1D3), .D4(REG1D4), .D5(REG1D5), .D6(REG1D6), .D7(REG1D7), .D8(REG1D8), .D9(REG1D9), .D10(REG1D10),
    .D11(REG1D11), .D12(REG1D12), .CLR(in_19), .LD(LD1));
  REG13 reg13_7 (
    .CLOCK(CLK), .Q0(in_1), .Q1(in_2), .Q2(in_3), .Q3(in_4), .Q4(in_5), .Q5(in_6), .Q6(in_7), .Q7(in_8),
    .Q8(in_9), .Q9(in_10), .Q10(in_11), .Q11(in_12), .Q12(in_13), .D0(REG2D0), .D1(REG2D1), .D2(REG2D2),
    .D3(REG2D3), .D4(REG2D4), .D5(REG2D5), .D6(REG2D6), .D7(REG2D7), .D8(REG2D8), .D9(REG2D9), .D10(REG2D10),
    .D11(REG2D11), .D12(REG2D12), .CLR(in_19), .LD(LD2));
  Multiplexer #(.select(4), .width(13), .enable("false")) multiplexer_1 (
    .in0({REGD12, REGD11, REGD10, REGD9, REGD8, REGD7, REGD6, REGD5, REGD4, REGD3, REGD2, REGD1, REGD0}),
    .in1({REG1D12, REG1D11, REG1D10, REG1D9, REG1D8, REG1D7, REG1D6, REG1D5, REG1D4, REG1D3, REG1D2, REG1D1, REG1D0}),
    .in2({REG2D12, REG2D11, REG2D10, REG2D9, REG2D8, REG2D7, REG2D6, REG2D5, REG2D4, REG2D3, REG2D2, REG2D1, REG2D0}),
    .in3({REG3D12, REG3D11, REG3D10, REG3D9, REG3D8, REG3D7, REG3D6, REG3D5, REG3D4, REG3D3, REG3D2, REG3D1, REG3D0}),
    .in4({REG4D12, REG4D11, REG4D10, REG4D9, REG4D8, REG4D7, REG4D6, REG4D5, REG4D4, REG4D3, REG4D2, REG4D1, REG4D0}),
    .in5({REG5D12, REG5D11, REG5D10, REG5D9, REG5D8, REG5D7, REG5D6, REG5D5, REG5D4, REG5D3, REG5D2, REG5D1, REG5D0}),
    .in6({REG6D12, REG6D11, REG6D10, REG6D9, REG6D8, REG6D7, REG6D6, REG6D5, REG6D4, REG6D3, REG6D2, REG6D1, REG6D0}),
    .in7({REG7D12, REG7D11, REG7D10, REG7D9, REG7D8, REG7D7, REG7D6, REG7D5, REG7D4, REG7D3, REG7D2, REG7D1, REG7D0}),
    .in8({REG8D12, REG8D11, REG8D10, REG8D9, REG8D8, REG8D7, REG8D6, REG8D5, REG8D4, REG8D3, REG8D2, REG8D1, REG8D0}),
    .in9({REG9D12, REG9D11, REG9D10, REG9D9, REG9D8, REG9D7, REG9D6, REG9D5, REG9D4, REG9D3, REG9D2, REG9D1, REG9D0}),
    .in10({REG10D12, REG10D11, REG10D10, REG10D9, REG10D8, REG10D7, REG10D6, REG10D5, REG10D4, REG10D3, REG10D2, REG10D1, REG10D0}),
    .in11({REG11D12, REG11D11, REG11D10, REG11D9, REG11D8, REG11D7, REG11D6, REG11D5, REG11D4, REG11D3, REG11D2, REG11D1, REG11D0}),
    .in12({REG12D12, REG12D11, REG12D10, REG12D9, REG12D8, REG12D7, REG12D6, REG12D5, REG12D4, REG12D3, REG12D2, REG12D1, REG12D0}),
    .in13({REG13D12, REG13D11, REG13D10, REG13D9, REG13D8, REG13D7, REG13D6, REG13D5, REG13D4, REG13D3, REG13D2, REG13D1, REG13D0}),
    .in14({REG14D12, REG14D11, REG14D10, REG14D9, REG14D8, REG14D7, REG14D6, REG14D5, REG14D4, REG14D3, REG14D2, REG14D1, REG14D0}),
    .in15({REG15D12, REG15D11, REG15D10, REG15D9, REG15D8, REG15D7, REG15D6, REG15D5, REG15D4, REG15D3, REG15D2, REG15D1, REG15D0}),
    .out({RD12, RD11, RD10, RD9, RD8, RD7, RD6, RD5, RD4, RD3, RD2, RD1, RD0}),
    .sel({in_23, in_22, in_21, in_20}));
  REG13 reg13_8 (
    .CLOCK(CLK), .Q0(in_1), .Q1(in_2), .Q2(in_3), .Q3(in_4), .Q4(in_5), .Q5(in_6), .Q6(in_7), .Q7(in_8),
    .Q8(in_9), .Q9(in_10), .Q10(in_11), .Q11(in_12), .Q12(in_13), .D0(REG9D0), .D1(REG9D1), .D2(REG9D2),
    .D3(REG9D3), .D4(REG9D4), .D5(REG9D5), .D6(REG9D6), .D7(REG9D7), .D8(REG9D8), .D9(REG9D9), .D10(REG9D10),
    .D11(REG9D11), .D12(REG9D12), .CLR(in_19), .LD(LD9));
  REG13 reg13_9 (
    .CLOCK(CLK), .Q0(in_1), .Q1(in_2), .Q2(in_3), .Q3(in_4), .Q4(in_5), .Q5(in_6), .Q6(in_7), .Q7(in_8),
    .Q8(in_9), .Q9(in_10), .Q10(in_11), .Q11(in_12), .Q12(in_13), .D0(REG10D0), .D1(REG10D1), .D2(REG10D2),
    .D3(REG10D3), .D4(REG10D4), .D5(REG10D5), .D6(REG10D6), .D7(REG10D7), .D8(REG10D8), .D9(REG10D9),
    .D10(REG10D10), .D11(REG10D11), .D12(REG10D12), .CLR(in_19), .LD(LD10));
  REG13 reg13_10 (
    .CLOCK(CLK), .Q0(in_1), .Q1(in_2), .Q2(in_3), .Q3(in_4), .Q4(in_5), .Q5(in_6), .Q6(in_7), .Q7(in_8),
    .Q8(in_9), .Q9(in_10), .Q10(in_11), .Q11(in_12), .Q12(in_13), .D0(REG11D0), .D1(REG11D1), .D2(REG11D2),
    .D3(REG11D3), .D4(REG11D4), .D5(REG11D5), .D6(REG11D6), .D7(REG11D7), .D8(REG11D8), .D9(REG11D9),
    .D10(REG11D10), .D11(REG11D11), .D12(REG11D12), .CLR(in_19), .LD(LD11));
  REG13 reg13_11 (
    .CLOCK(CLK), .Q0(in_1), .Q1(in_2), .Q2(in_3), .Q3(in_4), .Q4(in_5), .Q5(in_6), .Q6(in_7), .Q7(in_8),
    .Q8(in_9), .Q9(in_10), .Q10(in_11), .Q11(in_12), .Q12(in_13), .D0(REG12D0), .D1(REG12D1), .D2(REG12D2),
    .D3(REG12D3), .D4(REG12D4), .D5(REG12D5), .D6(REG12D6), .D7(REG12D7), .D8(REG12D8), .D9(REG12D9),
    .D10(REG12D10), .D11(REG12D11), .D12(REG12D12), .CLR(in_19), .LD(LD12));
  REG13 reg13_12 (
    .CLOCK(CLK), .Q0(in_1), .Q1(in_2), .Q2(in_3), .Q3(in_4), .Q4(in_5), .Q5(in_6), .Q6(in_7), .Q7(in_8),
    .Q8(in_9), .Q9(in_10), .Q10(in_11), .Q11(in_12), .Q12(in_13), .D0(REG13D0), .D1(REG13D1), .D2(REG13D2),
    .D3(REG13D3), .D4(REG13D4), .D5(REG13D5), .D6(REG13D6), .D7(REG13D7), .D8(REG13D8), .D9(REG13D9),
    .D10(REG13D10), .D11(REG13D11), .D12(REG13D12), .CLR(in_19), .LD(LD13));
  REG13 reg13_13 (
    .CLOCK(CLK), .Q0(in_1), .Q1(in_2), .Q2(in_3), .Q3(in_4), .Q4(in_5), .Q5(in_6), .Q6(in_7), .Q7(in_8),
    .Q8(in_9), .Q9(in_10), .Q10(in_11), .Q11(in_12), .Q12(in_13), .D0(REG7D0), .D1(REG7D1), .D2(REG7D2),
    .D3(REG7D3), .D4(REG7D4), .D5(REG7D5), .D6(REG7D6), .D7(REG7D7), .D8(REG7D8), .D9(REG7D9), .D10(REG7D10),
    .D11(REG7D11), .D12(REG7D12), .CLR(in_19), .LD(LD7));
  REG13 reg13_14 (
    .CLOCK(CLK), .Q0(in_1), .Q1(in_2), .Q2(in_3), .Q3(in_4), .Q4(in_5), .Q5(in_6), .Q6(in_7), .Q7(in_8),
    .Q8(in_9), .Q9(in_10), .Q10(in_11), .Q11(in_12), .Q12(in_13), .D0(REG8D0), .D1(REG8D1), .D2(REG8D2),
    .D3(REG8D3), .D4(REG8D4), .D5(REG8D5), .D6(REG8D6), .D7(REG8D7), .D8(REG8D8), .D9(REG8D9), .D10(REG8D10),
    .D11(REG8D11), .D12(REG8D12), .CLR(in_19), .LD(LD8));
  Demultiplexer #(.select(4), .enable("false")) demultiplexer_2 (
    .out0(D0), .out1(D1), .out2(D2), .out3(D3), .out4(D4), .out5(D5), .out6(D6), .out7(D7), .out8(D8),
    .out9(D9), .out10(D10), .out11(D11), .out12(D12), .out13(D13), .out14(D14), .out15(D15), .in(1'b1),
    .sel({in_23, in_22, in_21, in_20}));
  REG13 reg13_15 (
    .CLOCK(CLK), .Q0(in_1), .Q1(in_2), .Q2(in_3), .Q3(in_4), .Q4(in_5), .Q5(in_6), .Q6(in_7), .Q7(in_8),
    .Q8(in_9), .Q9(in_10), .Q10(in_11), .Q11(in_12), .Q12(in_13), .D0(REG14D0), .D1(REG14D1), .D2(REG14D2),
    .D3(REG14D3), .D4(REG14D4), .D5(REG14D5), .D6(REG14D6), .D7(REG14D7), .D8(REG14D8), .D9(REG14D9),
    .D10(REG14D10), .D11(REG14D11), .D12(REG14D12), .CLR(in_19), .LD(LD14));
  REG13 reg13_16 (
    .CLOCK(CLK), .Q0(in_1), .Q1(in_2), .Q2(in_3), .Q3(in_4), .Q4(in_5), .Q5(in_6), .Q6(in_7), .Q7(in_8),
    .Q8(in_9), .Q9(in_10), .Q10(in_11), .Q11(in_12), .Q12(in_13), .D0(REG15D0), .D1(REG15D1), .D2(REG15D2),
    .D3(REG15D3), .D4(REG15D4), .D5(REG15D5), .D6(REG15D6), .D7(REG15D7), .D8(REG15D8), .D9(REG15D9),
    .D10(REG15D10), .D11(REG15D11), .D12(REG15D12), .CLR(in_19), .LD(LD15));

  // Other names for the same wires on the sheet: W0 = in_15; W1 = in_16; W2 = in_17; W3 = in_18; R0 = in_20;
  //   R1 = in_21; R2 = in_22; R3 = in_23; CLR = in_19; WD0 = in_1; WD1 = in_2; WD2 = in_3; WD3 = in_4; WD4 = in_5;
  //   WD5 = in_6; WD6 = in_7; WD7 = in_8; WD8 = in_9; WD9 = in_10; WD10 = in_11; WD11 = in_12; WD12 = in_13;
  //   WR = in_14
endmodule

module REG13 (
  input  LD,
  input  CLOCK,
  input  Q0,
  input  Q1,
  input  Q2,
  input  Q3,
  input  Q4,
  input  Q5,
  input  Q6,
  input  CLR,
  input  Q7,
  input  Q8,
  input  Q9,
  input  Q10,
  input  Q11,
  input  Q12,
  output D0,
  output D1,
  output D2,
  output D3,
  output D4,
  output D5,
  output D6,
  output D7,
  output D8,
  output D9,
  output D10,
  output D11,
  output D12
);

  D_Flip_Flop #(.enable("true")) d_ff_1 (.clk(CLOCK), .D(Q0), .Q(D0), .en(LD), .reset(CLR));  // open: Qn, preset
  D_Flip_Flop #(.enable("true")) d_ff_2 (.clk(CLOCK), .D(Q7), .Q(D7), .en(LD), .reset(CLR));  // open: Qn, preset
  D_Flip_Flop #(.enable("true")) d_ff_3 (.clk(CLOCK), .D(Q1), .Q(D1), .en(LD), .reset(CLR));  // open: Qn, preset
  D_Flip_Flop #(.enable("true")) d_ff_4 (.clk(CLOCK), .D(Q8), .Q(D8), .en(LD), .reset(CLR));  // open: Qn, preset
  D_Flip_Flop #(.enable("true")) d_ff_5 (.clk(CLOCK), .D(Q2), .Q(D2), .en(LD), .reset(CLR));  // open: Qn, preset
  D_Flip_Flop #(.enable("true")) d_ff_6 (.clk(CLOCK), .D(Q9), .Q(D9), .en(LD), .reset(CLR));  // open: Qn, preset
  D_Flip_Flop #(.enable("true")) d_ff_7 (.clk(CLOCK), .D(Q3), .Q(D3), .en(LD), .reset(CLR));  // open: Qn, preset
  D_Flip_Flop #(.enable("true")) d_ff_8 (.clk(CLOCK), .D(Q10), .Q(D10), .en(LD), .reset(CLR));  // open: Qn, preset
  D_Flip_Flop #(.enable("true")) d_ff_9 (.clk(CLOCK), .D(Q4), .Q(D4), .en(LD), .reset(CLR));  // open: Qn, preset
  D_Flip_Flop #(.enable("true")) d_ff_10 (.clk(CLOCK), .D(Q11), .Q(D11), .en(LD), .reset(CLR));  // open: Qn, preset
  D_Flip_Flop #(.enable("true")) d_ff_11 (.clk(CLOCK), .D(Q5), .Q(D5), .en(LD), .reset(CLR));  // open: Qn, preset
  D_Flip_Flop #(.enable("true")) d_ff_12 (.clk(CLOCK), .D(Q12), .Q(D12), .en(LD), .reset(CLR));  // open: Qn, preset
  D_Flip_Flop #(.enable("true")) d_ff_13 (.clk(CLOCK), .D(Q6), .Q(D6), .en(LD), .reset(CLR));  // open: Qn, preset
endmodule
