// Logisim project MEF_ISAAC.circ as structural Verilog: 8 circuits, main circuit main
module main (
  input  ADD,
  input  PWR,
  input  V0,
  input  V1,
  input  V2,
  input  V3,
  input  V4,
  input  V5,
  input  S10,
  input  in_10,
  input  in_11,
  input  in_12,
  input  in_13,
  input  in_14,
  input  S20,
  input  in_16,
  input  in_17,
  input  in_18,
  input  in_19,
  input  in_20,
  input  S30,
  input  in_22,
  input  in_23,
  input  in_24,
  input  in_25,
  input  in_26
);

  wire and_1_out, and_2_out, and_3_out, CLOCK, comparador18bit_1_senha1, comparador18bit_1_senha2,
       comparador18bit_1_senha3, D0, D1, D2, D3, d_ff_2_q, d_ff_3_q, d_ff_4_q, d_ff_5_q, d_ff_7_q, d_ff_8_q,
       d_ff_10_q, d_ff_11_q, d_ff_14_q, d_ff_15_q, d_ff_16_q, d_ff_17_q, d_ff_18_q, d_ff_19_q, d_ff_20_q,
       d_ff_21_q, d_ff_22_q, d_ff_23_q, d_ff_24_q, d_ff_25_q, d_ff_26_q, d_ff_27_q, d_ff_28_q, d_ff_29_q,
       d_ff_31_q, DDEF0, DDEF1, DDEF2, DDEF3, DDEF4, DDEF5, DDEF6, DEZ0, DEZ1, DEZ2, DEZ3, DEZ4, DEZ5, DEZ6,
       DISPLAY, not_1_out, not_2_out, not_3_out, OUT, Q0, Q1, Q2, Q3, registrador18bits_1_out_10,
       registrador18bits_1_out_11, registrador18bits_1_out_12, registrador18bits_1_out_13,
       registrador18bits_1_r0, registrador18bits_1_r5, registrador18bits_2_out_10,
       registrador18bits_2_out_11, registrador18bits_2_out_12, registrador18bits_2_out_13,
       registrador18bits_2_r0, registrador18bits_2_r5, registrador18bits_3_out_10,
       registrador18bits_3_out_11, registrador18bits_3_out_12, registrador18bits_3_out_13,
       registrador18bits_3_r0, registrador18bits_3_r5, SENHA, T5, T20, TD5, TD20, TESTE, UDEF0, UDEF1, UDEF2,
       UDEF3, UDEF4, UDEF5, UDEF6, UNI0, UNI1, UNI2, UNI3, UNI4, UNI5, UNI6;
  wire [6:0] multiplexer_1_out, multiplexer_2_out;

  and and_1 (and_1_out, Q1, Q0);
  not not_1 (not_1_out, Q1);
  and and_2 (and_2_out, not_1_out, Q0);
  not not_2 (not_2_out, Q0);
  and and_3 (and_3_out, not_2_out, not_3_out);
  not not_3 (not_3_out, Q1);
  REGISTRADOR18BITS registrador18bits_1 (
    .V0(V0), .V1(V1), .V2(V2), .V3(V3), .V4(V4), .V5(V5), .CLOCK(CLOCK), .R0(registrador18bits_1_r0),
    .out_10(registrador18bits_1_out_10), .out_11(registrador18bits_1_out_11),
    .out_12(registrador18bits_1_out_12), .out_13(registrador18bits_1_out_13), .R5(registrador18bits_1_r5),
    .ON(and_1_out));
  REGISTRADOR18BITS registrador18bits_2 (
    .V0(V0), .V1(V1), .V2(V2), .V3(V3), .V4(V4), .V5(V5), .CLOCK(CLOCK), .R0(registrador18bits_2_r0),
    .out_10(registrador18bits_2_out_10), .out_11(registrador18bits_2_out_11),
    .out_12(registrador18bits_2_out_12), .out_13(registrador18bits_2_out_13), .R5(registrador18bits_2_r5),
    .ON(and_2_out));
  REGISTRADOR18BITS registrador18bits_3 (
    .V0(V0), .V1(V1), .V2(V2), .V3(V3), .V4(V4), .V5(V5), .CLOCK(CLOCK), .R0(registrador18bits_3_r0),
    .out_10(registrador18bits_3_out_10), .out_11(registrador18bits_3_out_11),
    .out_12(registrador18bits_3_out_12), .out_13(registrador18bits_3_out_13), .R5(registrador18bits_3_r5),
    .ON(and_3_out));
  COMPARADOR18BIT comparador18bit_1 (
    .R10(registrador18bits_1_r0), .in_2(registrador18bits_1_out_10), .in_3(registrador18bits_1_out_11),
    .in_4(registrador18bits_1_out_12), .in_5(registrador18bits_1_out_13), .in_6(registrador18bits_1_r5),
    .S10(S10), .in_8(in_10), .in_9(in_11), .in_10(in_12), .in_11(in_13), .in_12(in_14),
    .R20(registrador18bits_2_r0), .in_14(registrador18bits_2_out_10), .in_15(registrador18bits_2_out_11),
    .in_16(registrador18bits_2_out_12), .in_17(registrador18bits_2_out_13), .in_18(registrador18bits_2_r5),
    .S20(S20), .in_20(in_16), .in_21(in_17), .in_22(in_18), .in_23(in_19), .in_24(in_20),
    .R30(registrador18bits_3_r0), .in_26(registrador18bits_3_out_10), .in_27(registrador18bits_3_out_11),
    .in_28(registrador18bits_3_out_12), .in_29(registrador18bits_3_out_13), .in_30(registrador18bits_3_r5),
    .S30(S30), .in_32(in_22), .in_33(in_23), .in_34(in_24), .in_35(in_25), .in_36(in_26),
    .SENHA1(comparador18bit_1_senha1), .SENHA2(comparador18bit_1_senha2), .SENHA3(comparador18bit_1_senha3));
  and and_4 (SENHA, comparador18bit_1_senha3, comparador18bit_1_senha2, comparador18bit_1_senha1);
  Estados estados_1 (
    .Q3(Q3), .Q2(Q2), .Q1(Q1), .Q0(Q0), .ADD(ADD), .PWR(PWR), .T5(T5), .T20(T20), .SENHA(SENHA), .D3(D3),
    .D2(D2), .D1(D1), .D0(D0), .OUT(OUT), .TD5(TD5), .TD20(TD20), .DISPLAY(DISPLAY));  // open: LEDR, LEDG, LEDB
  // RGBLed rgbled_1: pin names not known
  _7_Segment_Display u_7_segment_display_1 (.dp(DISPLAY));  // open: g, f, a, b, e, d, c
  _7_Segment_Display u_7_segment_display_2 (.dp(DISPLAY));  // open: g, f, a, b, e, d, c
  Multiplexer #(.width(7), .enable("false")) multiplexer_1 (
    .in0(7'b1001001), .in1(7'b0001000), .out(multiplexer_1_out), .sel(OUT));
  Multiplexer #(.width(7), .enable("false")) multiplexer_2 (
    .in0(7'b1001001), .in1(7'b0001000), .out(multiplexer_2_out), .sel(OUT));
  Multiplexer #(.width(7), .enable("false")) multiplexer_3 (
    .in0({DDEF6, DDEF5, DDEF4, DDEF3, DDEF2, DDEF1, DDEF0}), .in1(multiplexer_1_out),
    .out({DEZ6, DEZ5, DEZ4, DEZ3, DEZ2, DEZ1, DEZ0}), .sel(TESTE));
  Multiplexer #(.width(7), .enable("false")) multiplexer_4 (
    .in0({UDEF6, UDEF5, UDEF4, UDEF3, UDEF2, UDEF1, UDEF0}), .in1(multiplexer_2_out),
    .out({UNI6, UNI5, UNI4, UNI3, UNI2, UNI1, UNI0}), .sel(TESTE));
  Clock u_CLOCK (.out(CLOCK));
  D_Flip_Flop d_ff_1 (.clk(CLOCK), .D(D0), .Q(Q0));  // open: Qn, preset, reset
  D_Flip_Flop d_ff_2 (.clk(CLOCK), .D(TD5), .Q(d_ff_2_q), .reset(d_ff_15_q));  // open: Qn, preset
  D_Flip_Flop d_ff_3 (.clk(CLOCK), .D(TD20), .Q(d_ff_3_q), .reset(d_ff_31_q));  // open: Qn, preset
  D_Flip_Flop d_ff_4 (.clk(CLOCK), .D(d_ff_2_q), .Q(d_ff_4_q), .reset(d_ff_15_q));  // open: Qn, preset
  D_Flip_Flop d_ff_5 (.clk(CLOCK), .D(d_ff_3_q), .Q(d_ff_5_q), .reset(d_ff_31_q));  // open: Qn, preset
  D_Flip_Flop d_ff_6 (.clk(CLOCK), .D(D1), .Q(Q1));  // open: Qn, preset, reset
  D_Flip_Flop d_ff_7 (.clk(CLOCK), .D(d_ff_4_q), .Q(d_ff_7_q), .reset(d_ff_15_q));  // open: Qn, preset
  D_Flip_Flop d_ff_8 (.clk(CLOCK), .D(d_ff_5_q), .Q(d_ff_8_q), .reset(d_ff_31_q));  // open: Qn, preset
  D_Flip_Flop d_ff_9 (.clk(CLOCK), .D(D2), .Q(Q2));  // open: Qn, preset, reset
  D_Flip_Flop d_ff_10 (.clk(CLOCK), .D(d_ff_7_q), .Q(d_ff_10_q), .reset(d_ff_15_q));  // open: Qn, preset
  D_Flip_Flop d_ff_11 (.clk(CLOCK), .D(d_ff_8_q), .Q(d_ff_11_q), .reset(d_ff_31_q));  // open: Qn, preset
  D_Flip_Flop d_ff_12 (.clk(CLOCK), .D(D3), .Q(Q3));  // open: Qn, preset, reset
  D_Flip_Flop d_ff_13 (.clk(CLOCK), .D(d_ff_10_q), .Q(T5), .reset(d_ff_15_q));  // open: Qn, preset
  D_Flip_Flop d_ff_14 (.clk(CLOCK), .D(d_ff_11_q), .Q(d_ff_14_q), .reset(d_ff_31_q));  // open: Qn, preset
  D_Flip_Flop d_ff_15 (.clk(CLOCK), .D(T5), .Q(d_ff_15_q), .reset(d_ff_15_q));  // open: Qn, preset
  D_Flip_Flop d_ff_16 (.clk(CLOCK), .D(d_ff_14_q), .Q(d_ff_16_q), .reset(d_ff_31_q));  // open: Qn, preset
  D_Flip_Flop d_ff_17 (.clk(CLOCK), .D(d_ff_16_q), .Q(d_ff_17_q), .reset(d_ff_31_q));  // open: Qn, preset
  D_Flip_Flop d_ff_18 (.clk(CLOCK), .D(d_ff_17_q), .Q(d_ff_18_q), .reset(d_ff_31_q));  // open: Qn, preset
  D_Flip_Flop d_ff_19 (.clk(CLOCK), .D(d_ff_18_q), .Q(d_ff_19_q), .reset(d_ff_31_q));  // open: Qn, preset
  D_Flip_Flop d_ff_20 (.clk(CLOCK), .D(d_ff_19_q), .Q(d_ff_20_q), .reset(d_ff_31_q));  // open: Qn, preset
  D_Flip_Flop d_ff_21 (.clk(CLOCK), .D(d_ff_20_q), .Q(d_ff_21_q), .reset(d_ff_31_q));  // open: Qn, preset
  D_Flip_Flop d_ff_22 (.clk(CLOCK), .D(d_ff_21_q), .Q(d_ff_22_q), .reset(d_ff_31_q));  // open: Qn, preset
  D_Flip_Flop d_ff_23 (.clk(CLOCK), .D(d_ff_22_q), .Q(d_ff_23_q), .reset(d_ff_31_q));  // open: Qn, preset
  D_Flip_Flop d_ff_24 (.clk(CLOCK), .D(d_ff_23_q), .Q(d_ff_24_q), .reset(d_ff_31_q));  // open: Qn, preset
  D_Flip_Flop d_ff_25 (.clk(CLOCK), .D(d_ff_24_q), .Q(d_ff_25_q), .reset(d_ff_31_q));  // open: Qn, preset
  D_Flip_Flop d_ff_26 (.clk(CLOCK), .D(d_ff_25_q), .Q(d_ff_26_q), .reset(d_ff_31_q));  // open: Qn, preset
  D_Flip_Flop d_ff_27 (.clk(CLOCK), .D(d_ff_26_q), .Q(d_ff_27_q), .reset(d_ff_31_q));  // open: Qn, preset
  D_Flip_Flop d_ff_28 (.clk(CLOCK), .D(d_ff_27_q), .Q(d_ff_28_q), .reset(d_ff_31_q));  // open: Qn, preset
  D_Flip_Flop d_ff_29 (.clk(CLOCK), .D(d_ff_28_q), .Q(d_ff_29_q), .reset(d_ff_31_q));  // open: Qn, preset
  D_Flip_Flop d_ff_30 (.clk(CLOCK), .D(d_ff_29_q), .Q(T20), .reset(d_ff_31_q));  // open: Qn, preset
  D_Flip_Flop d_ff_31 (.clk(CLOCK), .D(T20), .Q(d_ff_31_q));  // open: Qn, preset, reset
endmodule

module Estados (
  input  Q3,
  input  Q2,
  input  Q1,
  input  Q0,
  input  ADD,
  input  PWR,
  input  T5,
  input  T20,
  input  SENHA,
  output D3,
  output D2,
  output D1,
  output D0,
  output LEDR,
  output LEDG,
  output LEDB,
  output OUT,
  output TD5,
  output TD20,
  output DISPLAY
);

  wire and_1_out, and_2_out, and_3_out, and_4_out, and_5_out, and_6_out, and_7_out, and_8_out, and_9_out,
       and_10_out, and_11_out, and_12_out, and_13_out, and_14_out, and_15_out, and_16_out, and_17_out,
       and_18_out, and_19_out, and_20_out, and_23_out, and_24_out, and_26_out, and_27_out, and_29_out,
       and_30_out, and_31_out, not_1_out, not_2_out, not_3_out, not_4_out, not_5_out, not_6_out, not_7_out,
       not_8_out, not_9_out, not_10_out, not_11_out, not_12_out, not_13_out, not_14_out, not_15_out,
       not_16_out, not_17_out, not_18_out, not_19_out, not_20_out, not_21_out, not_22_out, not_23_out,
       not_24_out, not_25_out, not_26_out, not_27_out, not_28_out, not_29_out, not_30_out, not_31_out,
       not_32_out, not_33_out, not_34_out, not_35_out, not_36_out, not_37_out, not_38_out, not_39_out,
       not_40_out, not_41_out, not_42_out, not_43_out, not_44_out, not_45_out, not_46_out, not_47_out,
       not_48_out, not_49_out, not_50_out, not_51_out, not_52_out, not_53_out, not_54_out, not_55_out,
       not_56_out, not_57_out, not_58_out, not_59_out, not_60_out, not_61_out, not_62_out, not_63_out,
       not_64_out, not_65_out, not_66_out, not_67_out, not_68_out, not_69_out, not_70_out, not_71_out,
       not_72_out, not_73_out, not_74_out, not_75_out, not_76_out;

  not not_1 (not_1_out, Q3);
  not not_2 (not_2_out, Q0);
  not not_3 (not_3_out, PWR);
  not not_4 (not_4_out, Q2);
  not not_5 (not_5_out, Q1);
  not not_6 (not_6_out, Q0);
  not not_7 (not_7_out, T5);
  not not_8 (not_8_out, Q2);
  not not_9 (not_9_out, Q1);
  not not_10 (not_10_out, Q0);
  not not_11 (not_11_out, Q2);
  not not_12 (not_12_out, Q1);
  not not_13 (not_13_out, T20);
  not not_14 (not_14_out, Q3);
  not not_15 (not_15_out, Q0);
  not not_16 (not_16_out, Q3);
  not not_17 (not_17_out, Q2);
  not not_18 (not_18_out, Q3);
  not not_19 (not_19_out, Q1);
  not not_20 (not_20_out, Q3);
  not not_21 (not_21_out, Q0);
  not not_22 (not_22_out, ADD);
  not not_23 (not_23_out, Q3);
  not not_24 (not_24_out, T5);
  not not_25 (not_25_out, Q3);
  not not_26 (not_26_out, Q1);
  not not_27 (not_27_out, Q3);
  not not_28 (not_28_out, Q2);
  not not_29 (not_29_out, Q0);
  not not_30 (not_30_out, Q3);
  not not_31 (not_31_out, Q0);
  not not_32 (not_32_out, ADD);
  not not_33 (not_33_out, Q3);
  not not_34 (not_34_out, T5);
  not not_35 (not_35_out, Q3);
  not not_36 (not_36_out, Q0);
  not not_37 (not_37_out, Q3);
  not not_38 (not_38_out, Q0);
  not not_39 (not_39_out, Q3);
  not not_40 (not_40_out, T5);
  not not_41 (not_41_out, Q3);
  not not_42 (not_42_out, Q2);
  not not_43 (not_43_out, Q0);
  not not_44 (not_44_out, Q3);
  not not_45 (not_45_out, Q1);
  not not_46 (not_46_out, Q0);
  not not_47 (not_47_out, Q2);
  not not_48 (not_48_out, Q1);
  not not_49 (not_49_out, Q0);
  not not_50 (not_50_out, Q2);
  not not_51 (not_51_out, Q1);
  not not_52 (not_52_out, T20);
  not not_53 (not_53_out, Q3);
  not not_54 (not_54_out, Q0);
  not not_55 (not_55_out, Q2);
  not not_56 (not_56_out, Q1);
  not not_57 (not_57_out, Q3);
  not not_58 (not_58_out, Q2);
  not not_59 (not_59_out, Q1);
  not not_60 (not_60_out, Q0);
  not not_61 (not_61_out, Q2);
  not not_62 (not_62_out, Q1);
  not not_63 (not_63_out, T5);
  not not_64 (not_64_out, Q3);
  not not_65 (not_65_out, T5);
  not not_66 (not_66_out, Q2);
  not not_67 (not_67_out, Q1);
  not not_68 (not_68_out, Q0);
  not not_69 (not_69_out, T5);
  not not_70 (not_70_out, Q2);
  not not_71 (not_71_out, Q1);
  not not_72 (not_72_out, T20);
  not not_73 (not_73_out, Q3);
  not not_74 (not_74_out, Q3);
  not not_75 (not_75_out, Q2);
  not not_76 (not_76_out, Q1);
  and and_1 (and_1_out, not_1_out, Q2, Q1, not_2_out, ADD, not_3_out);
  and and_2 (and_2_out, Q3, not_4_out, not_5_out, not_6_out, not_7_out);
  and and_3 (and_3_out, Q3, not_8_out, not_9_out, not_10_out, SENHA);
  and and_4 (and_4_out, Q3, not_11_out, not_12_out, Q0, not_13_out);
  and and_5 (and_5_out, not_14_out, Q1, not_15_out, PWR);
  and and_6 (and_6_out, not_16_out, not_17_out, Q1, Q0, T5);
  and and_7 (and_7_out, not_18_out, Q2, not_19_out);
  and and_8 (and_8_out, not_20_out, Q2, not_21_out, not_22_out);
  and and_9 (and_9_out, not_23_out, Q2, Q0, not_24_out);
  and and_10 (and_10_out, not_25_out, not_26_out, Q0, T5);
  and and_11 (and_11_out, not_27_out, not_28_out, Q1, not_29_out);
  and and_12 (and_12_out, not_30_out, Q1, not_31_out, not_32_out);
  and and_13 (and_13_out, not_33_out, Q1, Q0, not_34_out);
  and and_14 (and_14_out, not_35_out, Q2, not_36_out, PWR);
  and and_15 (and_15_out, not_37_out, not_38_out, PWR);
  and and_16 (and_16_out, not_39_out, Q0, not_40_out);
  and and_17 (and_17_out, not_41_out, not_42_out, Q1, not_43_out, ADD);
  and and_18 (and_18_out, not_44_out, Q2, not_45_out, not_46_out, ADD);
  and and_19 (and_19_out, Q3, not_47_out, not_48_out, not_49_out, T5, SENHA);
  and and_20 (and_20_out, Q3, not_50_out, not_51_out, Q0, not_52_out);
  and and_21 (LEDR, not_53_out, not_54_out);
  and and_22 (LEDG, Q3, not_55_out, not_56_out, Q0);
  and and_23 (and_23_out, not_57_out, Q0);
  and and_24 (and_24_out, Q3, not_58_out, not_59_out, not_60_out);
  and and_25 (OUT, Q3, not_61_out, not_62_out, Q0, not_63_out);
  and and_26 (and_26_out, not_64_out, Q0, not_65_out);
  and and_27 (and_27_out, Q3, not_66_out, not_67_out, not_68_out, not_69_out);
  and and_28 (TD20, Q3, not_70_out, not_71_out, Q0, not_72_out);
  and and_29 (and_29_out, not_73_out, Q1);
  and and_30 (and_30_out, not_74_out, Q2);
  and and_31 (and_31_out, Q3, not_75_out, not_76_out);
  or or_1 (D3, and_1_out, and_2_out, and_3_out, and_4_out);
  or or_2 (D2, and_5_out, and_6_out, and_7_out, and_8_out, and_9_out);
  or or_3 (D1, and_10_out, and_11_out, and_12_out, and_13_out, and_14_out);
  or or_4 (D0, and_15_out, and_16_out, and_17_out, and_18_out, and_19_out, and_20_out);
  or or_5 (LEDB, and_23_out, and_24_out);
  or or_6 (TD5, and_26_out, and_27_out);
  or or_7 (DISPLAY, and_29_out, and_30_out, and_31_out);
endmodule

module COMPARADOR18BIT (
  input  R10,
  input  in_2,
  input  in_3,
  input  in_4,
  input  in_5,
  input  in_6,
  input  S10,
  input  in_8,
  input  in_9,
  input  in_10,
  input  in_11,
  input  in_12,
  input  R20,
  input  in_14,
  input  in_15,
  input  in_16,
  input  in_17,
  input  in_18,
  input  S20,
  input  in_20,
  input  in_21,
  input  in_22,
  input  in_23,
  input  in_24,
  input  R30,
  input  in_26,
  input  in_27,
  input  in_28,
  input  in_29,
  input  in_30,
  input  S30,
  input  in_32,
  input  in_33,
  input  in_34,
  input  in_35,
  input  in_36,
  output SENHA1,
  output SENHA2,
  output SENHA3
);

  Comparator #(.width(6)) comparator_1 (
    .a({in_6, in_5, in_4, in_3, in_2, R10}), .b({in_12, in_11, in_10, in_9, in_8, S10}), .eq(SENHA1));  // open: gt, lt
  Comparator #(.width(6)) comparator_2 (
    .a({in_18, in_17, in_16, in_15, in_14, R20}), .b({in_24, in_23, in_22, in_21, in_20, S20}), .eq(SENHA2));  // open: gt, lt
  Comparator #(.width(6)) comparator_3 (
    .a({in_30, in_29, in_28, in_27, in_26, R30}), .b({in_36, in_35, in_34, in_33, in_32, S30}), .eq(SENHA3));  // open: gt, lt
endmodule

module REGISTRADOR18BITS (
  input  V0,
  input  V1,
  input  V2,
  input  V3,
  input  V4,
  input  V5,
  input  ON,
  input  CLOCK,
  output R0,
  output out_10,
  output out_11,
  output out_12,
  output out_13,
  output R5
);

  wire multiplexer_1_out, multiplexer_2_out, multiplexer_3_out, multiplexer_4_out, multiplexer_5_out,
       multiplexer_6_out;

  Multiplexer #(.enable("false")) multiplexer_1 (.in0(R0), .in1(V0), .out(multiplexer_1_out), .sel(ON));
  D_Flip_Flop d_ff_1 (.clk(CLOCK), .D(multiplexer_1_out), .Q(R0));  // open: Qn, preset, reset
  Multiplexer #(.enable("false")) multiplexer_2 (.in0(out_10), .in1(V1), .out(multiplexer_2_out), .sel(ON));
  D_Flip_Flop d_ff_2 (.clk(CLOCK), .D(multiplexer_2_out), .Q(out_10));  // open: Qn, preset, reset
  Multiplexer #(.enable("false")) multiplexer_3 (.in0(out_11), .in1(V2), .out(multiplexer_3_out), .sel(ON));
  D_Flip_Flop d_ff_3 (.clk(CLOCK), .D(multiplexer_3_out), .Q(out_11));  // open: Qn, preset, reset
  Multiplexer #(.enable("false")) multiplexer_4 (.in0(out_12), .in1(V3), .out(multiplexer_4_out), .sel(ON));
  D_Flip_Flop d_ff_4 (.clk(CLOCK), .D(multiplexer_4_out), .Q(out_12));  // open: Qn, preset, reset
  Multiplexer #(.enable("false")) multiplexer_5 (.in0(out_13), .in1(V4), .out(multiplexer_5_out), .sel(ON));
  D_Flip_Flop d_ff_5 (.clk(CLOCK), .D(multiplexer_5_out), .Q(out_13));  // open: Qn, preset, reset
  Multiplexer #(.enable("false")) multiplexer_6 (.in0(R5), .in1(V5), .out(multiplexer_6_out), .sel(ON));
  D_Flip_Flop d_ff_6 (.clk(CLOCK), .D(multiplexer_6_out), .Q(R5));  // open: Qn, preset, reset
endmodule

module DECODBCD (
  input  EN,
  input  A3,
  input  A2,
  input  A1,
  input  A0,
  output S3,
  output S2,
  output S1,
  output S0
);

  wire and_1_out, and_2_out, and_3_out, and_4_out, and_5_out, and_6_out, and_7_out, and_8_out, and_9_out,
       and_10_out, and_11_out, not_1_out, not_2_out, not_3_out, not_4_out, not_5_out, not_6_out, not_7_out,
       not_8_out;

  and and_1 (and_1_out, EN, A2, A0);
  and and_2 (and_2_out, EN, A2, A1);
  and and_3 (and_3_out, EN, A3);
  not not_1 (not_1_out, A1);
  not not_2 (not_2_out, A0);
  not not_3 (not_3_out, A2);
  not not_4 (not_4_out, A0);
  not not_5 (not_5_out, A3);
  not not_6 (not_6_out, A2);
  not not_7 (not_7_out, A0);
  not not_8 (not_8_out, A0);
  or or_1 (S3, and_1_out, and_2_out, and_3_out);
  and and_4 (and_4_out, EN, A2, not_1_out, not_2_out);
  and and_5 (and_5_out, EN, A3, A0);
  and and_6 (and_6_out, EN, not_3_out, A1);
  and and_7 (and_7_out, EN, A1, A0);
  and and_8 (and_8_out, EN, A3, not_4_out);
  and and_9 (and_9_out, EN, not_5_out, not_6_out, A0);
  and and_10 (and_10_out, EN, A2, A1, not_7_out);
  and and_11 (and_11_out, EN, A3, not_8_out);
  or or_2 (S2, and_4_out, and_5_out);
  or or_3 (S1, and_6_out, and_7_out, and_8_out);
  or or_4 (S0, and_9_out, and_10_out, and_11_out);
endmodule

module bin_bcd (
  input  A5,
  input  in_2,
  input  in_3,
  input  in_4,
  input  in_5,
  input  A0,
  input  EN,
  output S8,
  output out_9,
  output out_10,
  output out_11,
  output out_12,
  output out_13,
  output out_14,
  output S0
);

  wire decodbcd_1_s0, decodbcd_1_s1, decodbcd_1_s2, decodbcd_1_s3, decodbcd_2_s0, decodbcd_2_s1,
       decodbcd_2_s2, decodbcd_2_s3, decodbcd_3_s0, decodbcd_3_s1, decodbcd_3_s2, decodbcd_3_s3,
       decodbcd_4_s0, decodbcd_4_s1, decodbcd_4_s2, decodbcd_6_s0, decodbcd_6_s1, decodbcd_6_s2,
       decodbcd_6_s3;

  DECODBCD decodbcd_1 (
    .EN(1'b0), .A3(1'b0), .A2(1'b0), .A1(A5), .A0(EN), .S3(decodbcd_1_s3), .S2(decodbcd_1_s2),
    .S1(decodbcd_1_s1), .S0(decodbcd_1_s0));
  DECODBCD decodbcd_2 (
    .EN(decodbcd_1_s2), .A3(decodbcd_1_s1), .A2(decodbcd_1_s0), .A1(in_2), .A0(EN), .S3(decodbcd_2_s3),
    .S2(decodbcd_2_s2), .S1(decodbcd_2_s1), .S0(decodbcd_2_s0));
  DECODBCD decodbcd_3 (
    .EN(decodbcd_2_s2), .A3(decodbcd_2_s1), .A2(decodbcd_2_s0), .A1(in_3), .A0(EN), .S3(decodbcd_3_s3),
    .S2(decodbcd_3_s2), .S1(decodbcd_3_s1), .S0(decodbcd_3_s0));
  DECODBCD decodbcd_4 (
    .EN(1'b0), .A3(decodbcd_1_s3), .A2(decodbcd_2_s3), .A1(decodbcd_3_s3), .A0(decodbcd_3_s2),
    .S2(decodbcd_4_s2), .S1(decodbcd_4_s1), .S0(decodbcd_4_s0));  // open: S3
  DECODBCD decodbcd_5 (
    .EN(decodbcd_4_s2), .A3(decodbcd_4_s1), .A2(decodbcd_4_s0), .A1(decodbcd_6_s3), .A0(decodbcd_6_s2),
    .S2(S8), .S1(out_9), .S0(out_10));  // open: S3
  DECODBCD decodbcd_6 (
    .EN(decodbcd_3_s2), .A3(decodbcd_3_s1), .A2(decodbcd_3_s0), .A1(in_4), .A0(EN), .S3(decodbcd_6_s3),
    .S2(decodbcd_6_s2), .S1(decodbcd_6_s1), .S0(decodbcd_6_s0));
  DECODBCD decodbcd_7 (
    .EN(decodbcd_6_s2), .A3(decodbcd_6_s1), .A2(decodbcd_6_s0), .A1(in_5), .A0(EN), .S3(out_11), .S2(out_12),
    .S1(out_13), .S0(out_14));

  assign S0 = A0;
endmodule

module ABERTO (
  input  EN,
  input  ESTADO,
  output A,
  output B,
  output C,
  output D,
  output E,
  output F,
  output G
);

  and and_1 (G, EN, ESTADO);

  assign A = 1'b0;
  assign B = 1'b0;
  assign C = 1'b0;
  assign D = 1'b0;
  assign E = 1'b0;
  assign F = 1'b0;
endmodule

module CANCERLAR (
  input  EN,
  input  ESTADO,
  output A,
  output B,
  output C,
  output D,
  output E,
  output F,
  output G
);

  and and_1 (A, EN, ESTADO);
  and and_2 (D, EN, ESTADO);
  and and_3 (G, EN, ESTADO);

  assign B = 1'b0;
  assign C = 1'b0;
  assign E = 1'b0;
  assign F = 1'b0;
endmodule
